// Logisim project crc.circ as structural Verilog: 2 circuits, main circuit CRC
module CRC (
  input  [7:0] in_1,
  input  [3:0] in_2,
  output [10:0] out_3
);

  wire [0:0] crc4_8_out_4;
  wire [3:0] crc4_1_out_4, crc4_2_out_4, crc4_3_out_4, crc4_4_out_4, crc4_5_out_4, crc4_6_out_4, crc4_7_out_4;

  CRC4 crc4_1 (.in_1(in_1[7:4]), .in_2(in_1[3]), .in_3(in_2), .out_4(crc4_1_out_4));
  CRC4 crc4_2 (.in_1(crc4_1_out_4), .in_2(in_1[2]), .in_3(in_2), .out_4(crc4_2_out_4));
  CRC4 crc4_3 (.in_1(crc4_2_out_4), .in_2(in_1[1]), .in_3(in_2), .out_4(crc4_3_out_4));
  CRC4 crc4_4 (.in_1(crc4_3_out_4), .in_2(in_1[0]), .in_3(in_2), .out_4(crc4_4_out_4));
  CRC4 crc4_5 (.in_1(crc4_4_out_4), .in_2(1'b0), .in_3(in_2), .out_4(crc4_5_out_4));
  CRC4 crc4_6 (.in_1(crc4_5_out_4), .in_2(1'b0), .in_3(in_2), .out_4(crc4_6_out_4));
  CRC4 crc4_7 (.in_1(crc4_6_out_4), .in_2(1'b0), .in_3(in_2), .out_4(crc4_7_out_4));
  CRC4 crc4_8 (.in_1(crc4_7_out_4), .in_2(1'b0), .in_3(in_2), .out_4({out_3[2:0], crc4_8_out_4[0]}));

  assign out_3[10:3] = in_1;

  // Other names for the same wires on the sheet: div[3:0] = in_2
endmodule

module CRC4 (
  input  [3:0] in_1,
  input  in_2,
  input  [3:0] in_3,
  output [3:0] out_4
);

  wire [3:0] xor_1_out;
  wire [3:3] multiplexer_1_out;

  Multiplexer #(.width(4)) multiplexer_1 (
    .in0(in_1), .in1(xor_1_out), .out({multiplexer_1_out[3], out_4[3:1]}), .sel(in_1[3]));  // open: en
  assign xor_1_out = in_1 ^ in_3;  // XOR_Gate xor_1, 4 bits wide

  assign out_4[0] = in_2;
endmodule
