// Logisim project foti.circ as structural Verilog: 1 circuit, main circuit ftoi
module ftoi (
  input  [15:0] in_1,
  output [31:0] out_2
);

  wire comparator_1_eq, comparator_1_gt, comparator_1_lt, comparator_2_lt, comparator_3_eq;
  wire [1:0] priority_encoder_1_out;
  wire [4:0] exp_10, exp_01111, subtractor_2_out;
  wire [31:0] _1, _1_t, adder_1_out, bit_extender_1_out, multiplexer_2_out, multiplexer_3_out, not_1_out,
       shifter_1_out, shifter_2_out;

  assign bit_extender_1_out = {{21{1'b0}}, {1'b1, in_1[9:0]}};  // Bit_Extender bit_extender_1
  Multiplexer #(.width(32)) multiplexer_1 (.in0(32'h1), .in1({32{1'b1}}), .out(_1), .sel(in_1[15]));  // open: en
  Subtractor #(.width(5)) subtractor_1 (.a(exp_01111), .b(5'b01010), .out(exp_10));  // open: bin, bout
  Subtractor #(.width(5)) subtractor_2 (.a(5'b01010), .b(exp_01111), .out(subtractor_2_out));  // open: bin, bout
  Subtractor #(.width(5)) subtractor_3 (.a(in_1[14:10]), .b(5'b01111), .out(exp_01111));  // open: bin, bout
  Comparator #(.width(5)) comparator_1 (
    .a(exp_01111), .b({5{1'b0}}), .gt(comparator_1_gt), .eq(comparator_1_eq), .lt(comparator_1_lt));
  Comparator #(.width(5)) comparator_2 (.a(exp_10), .b({5{1'b0}}), .lt(comparator_2_lt));  // open: gt, eq
  Shifter #(.width(32)) shifter_1 (.in(bit_extender_1_out), .\dist (exp_10), .out(shifter_1_out));
  Shifter #(.width(32), .shift("lr")) shifter_2 (
    .in(bit_extender_1_out), .\dist (subtractor_2_out), .out(shifter_2_out));
  Priority_Encoder #(.select(2)) priority_encoder_1 (
    .in0(comparator_1_gt), .in1(comparator_1_eq), .in2(comparator_1_lt), .in3(1'b0),
    .out(priority_encoder_1_out));  // open: gs, en_out, en_in
  Multiplexer #(.width(32)) multiplexer_2 (
    .in0(shifter_1_out), .in1(shifter_2_out), .out(multiplexer_2_out), .sel(comparator_2_lt));  // open: en
  Multiplexer #(.select(2), .width(32)) multiplexer_3 (
    .in0(_1_t), .in1(_1), .in2({32{1'b0}}), .out(multiplexer_3_out), .sel(priority_encoder_1_out));  // open: in3, en
  assign not_1_out = ~multiplexer_2_out;  // NOT_Gate not_1, 32 bits wide
  Comparator #(.width(5)) comparator_3 (.a(in_1[14:10]), .b({5{1'b1}}), .eq(comparator_3_eq));  // open: gt, lt
  Adder #(.width(32)) adder_1 (.a(not_1_out), .b(32'h1), .out(adder_1_out));  // open: cin, cout
  Multiplexer #(.width(32)) multiplexer_4 (
    .in0(multiplexer_3_out), .in1({32{1'b0}}), .out(out_2), .sel(comparator_3_eq));  // open: en
  Multiplexer #(.width(32)) multiplexer_5 (
    .in0(multiplexer_2_out), .in1(adder_1_out), .out(_1_t), .sel(in_1[15]));  // open: en

  // Other names for the same wires on the sheet: frac[9:0] = in_1[9:0]; exp[4:0] = in_1[14:10]; s = in_1[15]
endmodule
