// Logisim project fsm(Q4).circ as structural Verilog: 2 circuits, main circuit fsm
// in
module fsm (
  input  in_1,
  input  [1:0] in,
  output out_3
);

  wire clock_1_out, comparator_1_eq, comparator_2_eq, comparator_3_eq, or_1_out;
  wire [2:0] multiplexer_1_out, nstate_1_nst, st;

  Nstate nstate_1 (.in_1(in), .in_2(st), .nst(nstate_1_nst));
  Multiplexer #(.width(3)) multiplexer_1 (
    .in0(nstate_1_nst), .in1(3'b000), .out(multiplexer_1_out), .sel(in_1));  // open: en
  // Probe on st
  Register #(.width(3)) register_1 (.D(multiplexer_1_out), .Q(st), .clk(clock_1_out));  // open: en, clr
  Clock clock_1 (.out(clock_1_out));
  Comparator #(.width(3), .mode("unsigned")) comparator_1 (.a(st), .b(3'b011), .eq(comparator_1_eq));  // open: gt, lt
  Comparator #(.width(2), .mode("unsigned")) comparator_2 (.a(in), .b(2'b00), .eq(comparator_2_eq));  // open: gt, lt
  Comparator #(.width(2), .mode("unsigned")) comparator_3 (.a(in), .b(2'b10), .eq(comparator_3_eq));  // open: gt, lt
  and and_1 (out_3, comparator_1_eq, or_1_out);
  or or_1 (or_1_out, comparator_2_eq, comparator_3_eq);

  // Other names for the same wires on the sheet: clr = in_1
endmodule

module Nstate (
  input  [1:0] in_1,
  input  [2:0] in_2,
  output [2:0] nst
);

  wire comparator_1_eq;
  wire [2:0] multiplexer_1_out, multiplexer_2_out, multiplexer_3_out, multiplexer_4_out, multiplexer_5_out;

  Multiplexer #(.select(2), .width(3)) multiplexer_1 (
    .in0(3'b011), .in1(3'b000), .in2(3'b011), .in3(3'b000), .out(multiplexer_1_out), .sel(in_1));  // open: en
  Multiplexer #(.select(2), .width(3)) multiplexer_2 (
    .in0(3'b000), .in1(3'b001), .in2(3'b000), .in3(3'b000), .out(multiplexer_2_out), .sel(in_1));  // open: en
  Comparator #(.width(2), .mode("unsigned")) comparator_1 (.a(in_1), .b(2'b01), .eq(comparator_1_eq));  // open: gt, lt
  Multiplexer #(.width(3)) multiplexer_3 (
    .in0(3'b000), .in1(3'b001), .out(multiplexer_3_out), .sel(comparator_1_eq));  // open: en
  Multiplexer #(.select(2), .width(3)) multiplexer_4 (
    .in0(3'b011), .in1(3'b010), .in2(3'b011), .in3(3'b000), .out(multiplexer_4_out), .sel(in_1));  // open: en
  Multiplexer #(.select(2), .width(3)) multiplexer_5 (
    .in0(3'b100), .in1(3'b000), .in2(3'b100), .in3(3'b000), .out(multiplexer_5_out), .sel(in_1));  // open: en
  Multiplexer #(.select(3), .width(3)) multiplexer_6 (
    .in0(multiplexer_3_out), .in1(multiplexer_4_out), .in2(multiplexer_1_out), .in3(multiplexer_5_out),
    .in4(multiplexer_2_out), .out(nst), .sel(in_2));  // open: in5, in6, in7, en

  // Other names for the same wires on the sheet: in[1:0] = in_1; st[2:0] = in_2
endmodule
