// Logisim project moorea and mealy.circ as structural Verilog: 3 circuits, main circuit main
module main (
  input  in_1,
  input  in_2,
  output out_3,
  output out_4
);

  wire clock_1_out, clock_2_out, nstate_1_out_3, nstate_2_out_3, register_1_q, register_2_q, register_3_q;

  Nstate nstate_1 (.in_1(in_1), .in_2(register_1_q), .out_3(nstate_1_out_3));
  Nstate nstate_2 (.in_1(in_2), .in_2(register_3_q), .out_3(nstate_2_out_3));
  Register #(.width(1)) register_1 (.D(nstate_1_out_3), .Q(register_1_q), .clk(clock_1_out));  // open: en, clr
  Clock clock_1 (.out(clock_1_out));
  Register #(.width(1)) register_2 (.D(in_2), .Q(register_2_q), .clk(clock_2_out));  // open: en, clr
  Register #(.width(1)) register_3 (.D(nstate_2_out_3), .Q(register_3_q), .clk(clock_2_out));  // open: en, clr
  Clock clock_2 (.out(clock_2_out));
  Output output_1 (.in_1(in_1), .in_2(register_1_q), .out_3(out_3));
  Output output_2 (.in_1(register_2_q), .in_2(register_3_q), .out_3(out_4));

  // Notes on the sheet:
  //   Mealy
  //   Moore(can have more than 1 state)
  //   The most distinguished difference between moore and mealy
  //   is not that output depends on input and state
  //   but that output can vary multiple times as input changes within a circle
endmodule

module Nstate (
  input  in_1,
  input  in_2,
  output out_3
);


  // Notes on the sheet:
  //   The most distinguished difference between moore and mealy
  //   is not that output depends on input and state
  //   but that output can vary multiple times as input changes within a circle
endmodule

module Output (
  input  in_1,
  input  in_2,
  output out_3
);
endmodule
