// Logisim project nav.circ as structural Verilog: 4 circuits, main circuit navigation
module navigation (
  input  in_1,
  input  in_2,
  input  reset,
  input  reset_2,
  input  in_5,
  output arr,
  output arr_2,
  output hit,
  output hit_2,
  output [1:0] out_10
);

  wire clock_1_out, clock_2_out, clock_3_out, out_1_hit;
  wire [1:0] ram_1_data, ram_2_data, ram_3_data;
  wire [2:0] nxt_st_1_out_3, nxt_st_2_out_3, register_2_q, register_4_q;
  wire [7:0] counter_1_q, counter_2_q, counter_3_q;

  Counter counter_1 (.Q(counter_1_q), .clk(clock_2_out), .clr(reset));  // open: load, D, count, carry
  Clock clock_1 (.out(clock_1_out));
  RAM #(.dataWidth(2)) ram_1 (.addr(counter_1_q), .data(ram_1_data));  // open: sel, clk, ld, clr
  Clock clock_2 (.out(clock_2_out));
  Counter counter_2 (.Q(counter_2_q), .clk(clock_1_out), .clr(in_5));  // open: load, D, count, carry
  nxt_st nxt_st_1 (.in_1(register_2_q), .in_2(ram_1_data), .out_3(nxt_st_1_out_3));
  Register #(.width(1)) register_1 (.D(out_1_hit), .Q(hit), .clk(clock_2_out), .clr(reset));  // open: en
  out out_1 (.in_1(nxt_st_1_out_3), .in_2(ram_1_data), .hit(out_1_hit));
  Register #(.width(3)) register_2 (.D(nxt_st_1_out_3), .Q(register_2_q), .clk(clock_2_out), .clr(reset));  // open: en
  // Probe on ram_2_data
  RAM #(.dataWidth(2)) ram_2 (.addr(counter_2_q), .data(ram_2_data));  // open: sel, clk, ld, clr
  Register #(.width(2)) register_3 (.D(ram_2_data), .Q(out_10), .clk(clock_1_out), .clr(in_5));  // open: en
  Comparator #(.width(3), .mode("unsigned")) comparator_1 (.a(3'b100), .b(register_2_q), .eq(arr));  // open: gt, lt
  Counter counter_3 (.Q(counter_3_q), .clk(clock_3_out), .clr(reset_2));  // open: load, D, count, carry
  Clock clock_3 (.out(clock_3_out));
  RAM #(.dataWidth(2)) ram_3 (.addr(counter_3_q), .data(ram_3_data));  // open: sel, clk, ld, clr
  nxt_st nxt_st_2 (.in_1(register_4_q), .in_2(ram_3_data), .out_3(nxt_st_2_out_3));
  Register #(.width(3)) register_4 (
    .D(nxt_st_2_out_3), .Q(register_4_q), .clk(clock_3_out), .clr(reset_2));  // open: en
  Comparator #(.width(3), .mode("unsigned")) comparator_2 (.a(3'b100), .b(register_4_q), .eq(arr_2));  // open: gt, lt
  out out_2 (.in_1(register_4_q), .in_2(ram_3_data), .hit(hit_2));
endmodule

module Nstate (
  input  [1:0] in_1,
  output [2:0] out_2
);

  wire comparator_1_eq;
  wire [2:0] _0, _1, _2, _3, _4, undriven;

  Multiplexer #(.width(3)) multiplexer_1 (.in0(3'b000), .in1(3'b001), .out(_0), .sel(comparator_1_eq));  // open: en
  Comparator #(.width(2)) comparator_1 (.a(in_1), .b(2'b00), .eq(comparator_1_eq));  // open: gt, lt
  Multiplexer #(.select(2), .width(3)) multiplexer_2 (.in0(3'b000), .out(_1), .sel(in_1));  // open: in1, in2, in3, en
  Multiplexer #(.select(3), .width(3)) multiplexer_3 (
    .in0(_0), .in1(_1), .in2(_2), .in3(_3), .in4(_4), .out(out_2), .sel(undriven));  // open: in5, in6, in7, en

  // Other names for the same wires on the sheet: dir[1:0] = in_1
endmodule

module nxt_st (
  input  [2:0] in_1,
  input  [1:0] in_2,
  output [2:0] out_3
);

  wire and_1_out, and_2_out, and_3_out, and_4_out, and_5_out, and_6_out, and_7_out, and_8_out, and_9_out,
       and_10_out, and_11_out, not_1_out, not_2_out, not_3_out, not_4_out, not_5_out, not_6_out, not_7_out,
       not_8_out, not_9_out, not_10_out, not_11_out, not_12_out, not_13_out, not_14_out, not_15_out,
       not_16_out, not_17_out;

  not not_1 (not_1_out, in_1[0]);
  not not_2 (not_2_out, in_2[1]);
  not not_3 (not_3_out, in_2[0]);
  not not_4 (not_4_out, in_2[1]);
  not not_5 (not_5_out, in_1[1]);
  not not_6 (not_6_out, in_2[1]);
  not not_7 (not_7_out, in_2[1]);
  not not_8 (not_8_out, in_2[0]);
  not not_9 (not_9_out, in_1[0]);
  not not_10 (not_10_out, in_2[1]);
  not not_11 (not_11_out, in_1[0]);
  not not_12 (not_12_out, in_2[0]);
  not not_13 (not_13_out, in_1[2]);
  not not_14 (not_14_out, in_1[1]);
  not not_15 (not_15_out, in_2[1]);
  not not_16 (not_16_out, in_2[0]);
  not not_17 (not_17_out, in_2[0]);
  and and_1 (and_1_out, in_1[1], not_1_out, not_2_out, not_3_out);
  and and_2 (and_2_out, in_1[1], in_1[0], not_4_out, in_2[0]);
  and and_3 (and_3_out, not_5_out, in_1[0], not_6_out);
  and and_4 (and_4_out, in_1[0], not_7_out, not_8_out);
  and and_5 (and_5_out, in_1[1], not_9_out, not_10_out, in_2[0]);
  and and_6 (and_6_out, in_1[1], not_11_out, in_2[1], not_12_out);
  and and_7 (and_7_out, in_1[1], in_1[0], in_2[1], in_2[0]);
  and and_8 (and_8_out, not_13_out, not_14_out, not_15_out, not_16_out);
  and and_9 (and_9_out, in_1[0], in_2[1], in_2[0]);
  and and_10 (and_10_out, in_1[1], in_2[1], in_2[0]);
  and and_11 (and_11_out, in_1[1], in_1[0], not_17_out);
  or or_1 (out_3[2], and_1_out, and_2_out);
  or or_2 (out_3[1], and_3_out, and_4_out, and_5_out, and_6_out, and_7_out);
  or or_3 (out_3[0], and_8_out, and_9_out, and_10_out, and_11_out);
endmodule

module out (
  input  [2:0] in_1,
  input  [1:0] in_2,
  output hit
);

  wire and_1_out, and_2_out, and_3_out, and_4_out, and_5_out, not_1_out, not_2_out, not_3_out, not_4_out,
       not_5_out, not_6_out, not_7_out, not_8_out, not_9_out, not_10_out, not_11_out;

  not not_1 (not_1_out, in_1[2]);
  not not_2 (not_2_out, in_1[0]);
  not not_3 (not_3_out, in_2[1]);
  not not_4 (not_4_out, in_1[2]);
  not not_5 (not_5_out, in_1[1]);
  not not_6 (not_6_out, in_1[0]);
  not not_7 (not_7_out, in_1[2]);
  not not_8 (not_8_out, in_1[0]);
  not not_9 (not_9_out, in_2[0]);
  not not_10 (not_10_out, in_2[1]);
  not not_11 (not_11_out, in_2[0]);
  and and_1 (and_1_out, not_1_out, not_2_out, not_3_out, in_2[0]);
  and and_2 (and_2_out, not_4_out, not_5_out, not_6_out, in_2[1]);
  and and_3 (and_3_out, not_7_out, not_8_out, in_2[1], not_9_out);
  and and_4 (and_4_out, in_1[0], in_2[1], in_2[0]);
  and and_5 (and_5_out, in_1[1], in_1[0], not_10_out, not_11_out);
  or or_1 (hit, and_1_out, and_2_out, and_3_out, and_4_out, and_5_out);
endmodule
