// Logisim project MD5.circ as structural Verilog: 1 circuit, main circuit main
module main (
  input  [31:0] in_1,
  output [31:0] out_2
);

  wire comparator_1_eq;
  wire [4:0] bitfinder_1_index, subtractor_1_out, subtractor_3_out;
  wire [31:0] adder_1_out, shifter_1_out, shifter_2_out;
  wire [31:27] multiplexer_1_out;

  BitFinder #(.width(32), .\type ("high1")) bitfinder_1 (.in(in_1), .index(bitfinder_1_index));  // open: found
  Shifter #(.width(32)) shifter_1 (.in(in_1), .\dist (subtractor_1_out), .out(shifter_1_out));
  Subtractor #(.width(5)) subtractor_1 (
    .a({5{1'b1}}), .b(bitfinder_1_index), .out(subtractor_1_out));  // open: bin, bout
  Subtractor #(.width(5)) subtractor_2 (.a(bitfinder_1_index), .b(5'b00100), .out(out_2[4:0]));  // open: bin, bout
  Subtractor #(.width(5)) subtractor_3 (.a(subtractor_1_out), .b(5'b00001), .out(subtractor_3_out));  // open: bin, bout
  Comparator #(.width(5)) comparator_1 (.a(subtractor_1_out), .b({5{1'b0}}), .eq(comparator_1_eq));  // open: gt, lt
  Shifter #(.width(32)) shifter_2 (.in(32'h1), .\dist (subtractor_3_out), .out(shifter_2_out));
  // Probe on {multiplexer_1_out, out_2[31:5]}
  Adder #(.width(32)) adder_1 (.a(shifter_1_out), .b(shifter_2_out), .out(adder_1_out));  // open: cin, cout
  Multiplexer #(.width(32)) multiplexer_1 (
    .in0(adder_1_out), .in1(shifter_1_out), .out({multiplexer_1_out, out_2[31:5]}), .sel(comparator_1_eq));  // open: en
endmodule
