// Logisim project base_change_bit_sel.circ as structural Verilog: 1 circuit, main circuit main
module main (
  input  [1:0] in_1,
  input  [8:0] in_2,
  output [3:0] out_3,
  output [3:0] out_4,
  output [3:0] out_5
);

  wire [3:0] _00out1, _00out2, _00out3, _01out3, _10out1, _10out2, _10out3;
  wire [8:0] divider_1_out, divider_2_out;
  wire [8:4] divider_1_rem, divider_2_rem, divider_3_rem;

  Divider #(.width(9)) divider_1 (
    .a(in_2), .b(9'ha), .out(divider_1_out), .rem({divider_1_rem, _10out1}));  // open: upper
  assign _00out1 = {{1{1'b0}}, in_2[2:0]};  // Bit_Extender bit_extender_1
  assign _00out2 = {{1{1'b0}}, in_2[5:3]};  // Bit_Extender bit_extender_2
  assign _00out3 = {{1{1'b0}}, in_2[8:6]};  // Bit_Extender bit_extender_3
  assign _01out3 = {{3{1'b0}}, in_2[8]};  // Bit_Extender bit_extender_4
  Divider #(.width(9)) divider_2 (
    .a(divider_1_out), .b(9'ha), .out(divider_2_out), .rem({divider_2_rem, _10out2}));  // open: upper
  Divider #(.width(9)) divider_3 (.a(divider_2_out), .b(9'ha), .rem({divider_3_rem, _10out3}));  // open: out, upper
  Multiplexer #(.select(2), .width(4)) multiplexer_1 (
    .in0(_00out1), .in1(in_2[3:0]), .in2(_10out1), .out(out_3), .sel(in_1));  // open: in3, en
  Multiplexer #(.select(2), .width(4)) multiplexer_2 (
    .in0(_00out2), .in1(in_2[7:4]), .in2(_10out2), .out(out_4), .sel(in_1));  // open: in3, en
  Multiplexer #(.select(2), .width(4)) multiplexer_3 (
    .in0(_00out3), .in1(_01out3), .in2(_10out3), .out(out_5), .sel(in_1));  // open: in3, en

  // Other names for the same wires on the sheet: _01out1[3:0] = in_2[3:0]; in[8:0] = in_2; _01out2[3:0] = in_2[7:4]
endmodule
