// Logisim project sell.circ as structural Verilog: 6 circuits, main circuit main
module main (
  input  in_1,
  input  [2:0] in_2,
  input  in_3,
  output out_4,
  output out_5,
  output out_6,
  output out_7
);

  wire nst_1_out_5, out_1_out_5, register_4_q;
  wire [2:0] out_1_out_4, register_1_q;
  wire [3:0] nst_1_out_4, register_3_q;

  // Probe on register_3_q
  out out_1 (.in_1(register_3_q), .in_2(in_2), .in_3(register_4_q), .out_4(out_1_out_4), .out_5(out_1_out_5));
  nst nst_1 (.in_1(register_3_q), .in_2(in_2), .in_3(register_4_q), .out_4(nst_1_out_4), .out_5(nst_1_out_5));
  // Probe on out_1_out_4
  Register #(.width(3)) register_1 (.D(out_1_out_4), .Q(register_1_q), .clk(in_1), .clr(in_3));  // open: en
  Register #(.width(1)) register_2 (.D(out_1_out_5), .Q(out_7), .clk(in_1), .clr(in_3));  // open: en
  Register #(.width(4)) register_3 (.D(nst_1_out_4), .Q(register_3_q), .clk(in_1), .clr(in_3));  // open: en
  Register #(.width(1)) register_4 (.D(nst_1_out_5), .Q(register_4_q), .clk(in_1), .clr(in_3));  // open: en
  exchange exchange_1 (.in_1(register_1_q), .out_2(out_4), .out_3(out_5), .out_4(out_6));
endmodule

module problem (
);


  // Notes on the sheet:
  //   题面大概是有一个售货机，你只能往里面不投币，投一元，投两元，投五元，只要大于等于5元就要使得出货信号dispense为1，然后找钱信号1,2,4相应的给出。题目要求异步复位，要求一旦出货之后，就需要让售货机下一个状态无条件变成初始的没有接收到钱的状态，并且忽略刚变回初始状态的时候的投币（应该是这样，题面有点记不清楚了），要求使用moore型状态机实现。
endmodule

module nst (
  input  [3:0] in_1,
  input  [2:0] in_2,
  input  in_3,
  output [3:0] out_4,
  output out_5
);

  wire comparator_1_lt, not_1_out;
  wire [3:0] adder_1_out, bit_extender_1_out;

  assign bit_extender_1_out = {{1{1'b0}}, in_2};  // Bit_Extender bit_extender_1
  Adder #(.width(4)) adder_1 (.a(in_1), .b(bit_extender_1_out), .out(adder_1_out));  // open: cin, cout
  Comparator #(.width(4), .mode("unsigned")) comparator_1 (
    .a(adder_1_out), .b(4'b0101), .lt(comparator_1_lt));  // open: gt, eq
  Multiplexer #(.width(4)) multiplexer_1 (
    .in0(4'b0000), .in1(adder_1_out), .out(out_4), .sel(comparator_1_lt));  // open: en
  not not_1 (not_1_out, comparator_1_lt);
  Multiplexer multiplexer_2 (.in0(not_1_out), .in1(1'b0), .out(out_5), .sel(in_3));  // open: en

  // Other names for the same wires on the sheet: rst = in_3
endmodule

module out (
  input  [3:0] in_1,
  input  [2:0] in_2,
  input  in_3,
  output [2:0] out_4,
  output out_5
);

  wire comparator_1_lt, or_1_out;
  wire [3:0] adder_1_out, bit_extender_1_out, subtractor_1_out;

  assign bit_extender_1_out = {{1{1'b0}}, in_2};  // Bit_Extender bit_extender_1
  Adder #(.width(4)) adder_1 (.a(in_1), .b(bit_extender_1_out), .out(adder_1_out));  // open: cin, cout
  Comparator #(.width(4), .mode("unsigned")) comparator_1 (
    .a(adder_1_out), .b(4'b0101), .lt(comparator_1_lt));  // open: gt, eq
  Subtractor #(.width(4)) subtractor_1 (.a(adder_1_out), .b(4'b0101), .out(subtractor_1_out));  // open: bin, bout
  or or_1 (or_1_out, comparator_1_lt, in_3);
  Multiplexer #(.width(3)) multiplexer_1 (
    .in0(subtractor_1_out[2:0]), .in1(3'b000), .out(out_4), .sel(or_1_out));  // open: en
  Multiplexer multiplexer_2 (.in0(1'b1), .in1(1'b0), .out(out_5), .sel(or_1_out));  // open: en
endmodule

module exchange (
  input  [2:0] in_1,
  output out_2,
  output out_3,
  output out_4
);

  Pull_Resistor pull_resistor_1 (.node(out_2));
  Multiplexer #(.select(3), .disabled(0)) multiplexer_1 (
    .in1(1'b0), .in2(1'b0), .in3(1'b0), .in4(1'b1), .out(out_2), .sel(in_1));  // open: in0, in5, in6, in7, en
  Pull_Resistor pull_resistor_2 (.node(out_3));
  Multiplexer #(.select(3), .disabled(0)) multiplexer_2 (
    .in1(1'b0), .in2(1'b1), .in3(1'b1), .in4(1'b0), .out(out_3), .sel(in_1));  // open: in0, in5, in6, in7, en
  Multiplexer #(.select(3), .disabled(0)) multiplexer_3 (
    .in1(1'b1), .in2(1'b0), .in3(1'b1), .in4(1'b0), .out(out_4), .sel(in_1));  // open: in0, in5, in6, in7, en
  Pull_Resistor pull_resistor_3 (.node(out_4));
endmodule

module test (
  input  in_1,
  output _4,
  output _2,
  output _1,
  output dispense
);

  wire clock_1_out, not_1_out;
  wire [2:0] ram_1_data;
  wire [7:0] counter_1_q;

  Clock clock_1 (.out(clock_1_out));
  not not_1 (not_1_out, clock_1_out);
  Counter counter_1 (.Q(counter_1_q), .clk(not_1_out), .clr(in_1));  // open: load, D, count, carry
  RAM #(.dataWidth(3)) ram_1 (.addr(counter_1_q), .data(ram_1_data));  // open: sel, clk, ld, clr
  main main_1 (
    .in_2(ram_1_data), .in_1(clock_1_out), .in_3(in_1), .out_4(_4), .out_5(_2), .out_6(_1), .out_7(dispense));
endmodule
