// Logisim project shift.circ as structural Verilog: 1 circuit, main circuit main
module main (
  input  [15:0] in_1,
  input  [3:0] in_2,
  output [15:0] out_3
);

  wire [0:0] multiplexer_3_out;
  wire [1:0] multiplexer_2_out;
  wire [3:0] multiplexer_1_out;
  wire [11:0] multiplexer_1_out_2;
  wire [13:0] multiplexer_2_out_2;
  wire [14:0] multiplexer_3_out_2;

  Multiplexer #(.width(16)) multiplexer_1 (
    .in0(in_1), .in1({{8{1'b0}}, in_1[15:8]}), .out({multiplexer_1_out_2, multiplexer_1_out}), .sel(in_2[3]));  // open: en
  Multiplexer #(.width(16)) multiplexer_2 (
    .in0({multiplexer_1_out_2, multiplexer_1_out}), .in1({4'b0000, multiplexer_1_out_2}),
    .out({multiplexer_2_out_2, multiplexer_2_out}), .sel(in_2[2]));  // open: en
  Multiplexer #(.width(16)) multiplexer_3 (
    .in0({multiplexer_2_out_2, multiplexer_2_out}), .in1({2'b00, multiplexer_2_out_2}),
    .out({multiplexer_3_out_2, multiplexer_3_out[0]}), .sel(in_2[1]));  // open: en
  Multiplexer #(.width(16)) multiplexer_4 (
    .in0({multiplexer_3_out_2, multiplexer_3_out[0]}), .in1({1'b0, multiplexer_3_out_2}), .out(out_3),
    .sel(in_2[0]));  // open: en
endmodule
