// Logisim project cpu1.circ as structural Verilog: 9 circuits, main circuit main
module main (
  input  in_1,
  output [31:0] out_2,
  output out_3,
  output [4:0] out_4,
  output [31:0] out_5,
  output out_6,
  output [4:0] out_7,
  output [31:0] out_8
);

  wire ALU_B_sel, clk, cmp, EXT_op;
  wire [1:0] RF_A3_sel, RF_WD_sel;
  wire [2:0] NPC_op;
  wire [3:0] ALU_op;
  wire [4:0] istr_15_11, istr_20_16, istr_25_21, Shamt;
  wire [15:0] imm16;
  wire [25:0] imm26;
  wire [31:0] ALU_C, DM_RD, EXTout, multiplexer_3_out, npc_1_out_6, PC4, PC_q, RF_RD1;

  Clock clock_1 (.out(clk));
  Register #(.width(32)) PC (.D(npc_1_out_6), .Q(PC_q), .clk(clk), .clr(in_1));  // open: en
  NPC npc_1 (.out_6(npc_1_out_6), .in_4(PC_q), .in_5(RF_RD1), .in_1(imm26), .in_2(NPC_op), .in_3(cmp), .PC4(PC4));
  IM im_1 (.in_1(PC_q), .out_2(out_2));
  SPLT splt_1 (
    .in_1(out_2), .out_2(imm26), .out_3(imm16), .out_4(istr_25_21), .out_5(istr_20_16), .out_6(istr_15_11),
    .out_7(Shamt));
  CTR ctr_1 (
    .in_1(out_2), .out_2(NPC_op), .out_3(out_3), .out_4(RF_A3_sel), .out_5(RF_WD_sel), .out_6(EXT_op),
    .out_7(ALU_op), .out_8(ALU_B_sel), .out_9(out_6));
  EXT ext_1 (.in_2(imm16), .out_3(EXTout), .in_1(EXT_op));
  Multiplexer #(.select(2), .width(5)) multiplexer_1 (
    .in0(istr_15_11), .in1(istr_20_16), .in2({5{1'b1}}), .out(out_4), .sel(RF_A3_sel));  // open: in3, en
  RF rf_1 (
    .A1(istr_25_21), .A2(istr_20_16), .A3(out_4), .out_8(RF_RD1), .out_9(out_8), .clk(out_3), .WE(clk),
    .reset(in_1), .in_7(out_5));
  Multiplexer #(.select(2), .width(32)) multiplexer_2 (
    .in0({ALU_C[31:7], out_7, ALU_C[1:0]}), .in1(DM_RD), .in2(PC4), .out(out_5), .sel(RF_WD_sel));  // open: in3, en
  Multiplexer #(.width(32)) multiplexer_3 (
    .in0(out_8), .in1(EXTout), .out(multiplexer_3_out), .sel(ALU_B_sel));  // open: en
  ALU alu_1 (
    .in_3(RF_RD1), .in_4(multiplexer_3_out), .out_5({ALU_C[31:7], out_7, ALU_C[1:0]}), .in_1(ALU_op),
    .in_2(Shamt), .out_6(cmp));
  DM dm_1 (.in_4(out_7), .out_6(DM_RD), .in_1(out_6), .in_2(clk), .in_3(in_1), .in_5(out_8));

  // Other names for the same wires on the sheet: ALU_C[6:2] = out_7; DMaddr[4:0] = out_7; DM_wr = out_6;
  //   Istr[31:0] = out_2; res = in_1; RF_RD2[31:0] = out_8; RF_WD[31:0] = out_5; RF_wr = out_3; RFaddr[4:0] = out_4

  // Notes on the sheet:
  //   CPU(mips sig_circ)
endmodule

module RF (
  input  clk,
  input  WE,
  input  reset,
  input  [4:0] A1,
  input  [4:0] A2,
  input  [4:0] A3,
  input  [31:0] in_7,
  output [31:0] out_8,
  output [31:0] out_9
);

  wire [31:0] in00, in01, in02, in03, in04, in05, in06, in07, in08, in09, in10, in11, in12, in13, in14, in15,
       in16, in17, in18, in19, in20, in21, in22, in23, in24, in25, in26, in27, in28, in29, in30, in31, out00,
       out01, out02, out03, out04, out05, out06, out07, out08, out09, out10, out11, out12, out13, out14,
       out15, out16, out17, out18, out19, out20, out21, out22, out23, out24, out25, out26, out27, out28,
       out29, out30, out31;

  Register #(.width(32)) register_1 (.D({32{1'b0}}), .en(WE), .Q(out00), .clk(clk), .clr(reset));
  Register #(.width(32)) register_2 (.D(in08), .en(WE), .Q(out08), .clk(clk), .clr(reset));
  Register #(.width(32)) register_3 (.D(in16), .en(WE), .Q(out16), .clk(clk), .clr(reset));
  Register #(.width(32)) register_4 (.D(in24), .en(WE), .Q(out24), .clk(clk), .clr(reset));
  Demultiplexer #(.select(5), .width(32), .tristate("true"), .enable("false")) demultiplexer_1 (
    .out0(in00), .out1(in01), .out2(in02), .out3(in03), .out4(in04), .out5(in05), .out6(in06), .out7(in07),
    .out8(in08), .out9(in09), .out10(in10), .out11(in11), .out12(in12), .out13(in13), .out14(in14),
    .out15(in15), .out16(in16), .out17(in17), .out18(in18), .out19(in19), .out20(in20), .out21(in21),
    .out22(in22), .out23(in23), .out24(in24), .out25(in25), .out26(in26), .out27(in27), .out28(in28),
    .out29(in29), .out30(in30), .out31(in31), .in(in_7), .sel(A3));
  Register #(.width(32)) register_5 (.D(in01), .en(WE), .Q(out01), .clk(clk), .clr(reset));
  Register #(.width(32)) register_6 (.D(in09), .en(WE), .Q(out09), .clk(clk), .clr(reset));
  Register #(.width(32)) register_7 (.D(in17), .en(WE), .Q(out17), .clk(clk), .clr(reset));
  Register #(.width(32)) register_8 (.D(in25), .en(WE), .Q(out25), .clk(clk), .clr(reset));
  Register #(.width(32)) register_9 (.D(in02), .en(WE), .Q(out02), .clk(clk), .clr(reset));
  Register #(.width(32)) register_10 (.D(in10), .en(WE), .Q(out10), .clk(clk), .clr(reset));
  Register #(.width(32)) register_11 (.D(in18), .en(WE), .Q(out18), .clk(clk), .clr(reset));
  Register #(.width(32)) register_12 (.D(in26), .en(WE), .Q(out26), .clk(clk), .clr(reset));
  Register #(.width(32)) register_13 (.D(in03), .en(WE), .Q(out03), .clk(clk), .clr(reset));
  Register #(.width(32)) register_14 (.D(in11), .en(WE), .Q(out11), .clk(clk), .clr(reset));
  Register #(.width(32)) register_15 (.D(in19), .en(WE), .Q(out19), .clk(clk), .clr(reset));
  Register #(.width(32)) register_16 (.D(in27), .en(WE), .Q(out27), .clk(clk), .clr(reset));
  Multiplexer #(.select(5), .width(32), .enable("false")) multiplexer_1 (
    .in0(out00), .in1(out01), .in2(out02), .in3(out03), .in4(out04), .in5(out05), .in6(out06), .in7(out07),
    .in8(out08), .in9(out09), .in10(out10), .in11(out11), .in12(out12), .in13(out13), .in14(out14),
    .in15(out15), .in16(out16), .in17(out17), .in18(out18), .in19(out19), .in20(out20), .in21(out21),
    .in22(out22), .in23(out23), .in24(out24), .in25(out25), .in26(out26), .in27(out27), .in28(out28),
    .in29(out29), .in30(out30), .in31(out31), .out(out_8), .sel(A1));
  Register #(.width(32)) register_17 (.D(in04), .en(WE), .Q(out04), .clk(clk), .clr(reset));
  Register #(.width(32)) register_18 (.D(in12), .en(WE), .Q(out12), .clk(clk), .clr(reset));
  Register #(.width(32)) register_19 (.D(in20), .en(WE), .Q(out20), .clk(clk), .clr(reset));
  Register #(.width(32)) register_20 (.D(in28), .en(WE), .Q(out28), .clk(clk), .clr(reset));
  Register #(.width(32)) register_21 (.D(in05), .en(WE), .Q(out05), .clk(clk), .clr(reset));
  Register #(.width(32)) register_22 (.D(in13), .en(WE), .Q(out13), .clk(clk), .clr(reset));
  Register #(.width(32)) register_23 (.D(in21), .en(WE), .Q(out21), .clk(clk), .clr(reset));
  Register #(.width(32)) register_24 (.D(in29), .en(WE), .Q(out29), .clk(clk), .clr(reset));
  Multiplexer #(.select(5), .width(32), .enable("false")) multiplexer_2 (
    .in0(out00), .in1(out01), .in2(out02), .in3(out03), .in4(out04), .in5(out05), .in6(out06), .in7(out07),
    .in8(out08), .in9(out09), .in10(out10), .in11(out11), .in12(out12), .in13(out13), .in14(out14),
    .in15(out15), .in16(out16), .in17(out17), .in18(out18), .in19(out19), .in20(out20), .in21(out21),
    .in22(out22), .in23(out23), .in24(out24), .in25(out25), .in26(out26), .in27(out27), .in28(out28),
    .in29(out29), .in30(out30), .in31(out31), .out(out_9), .sel(A2));
  Register #(.width(32)) register_25 (.D(in06), .en(WE), .Q(out06), .clk(clk), .clr(reset));
  Register #(.width(32)) register_26 (.D(in14), .en(WE), .Q(out14), .clk(clk), .clr(reset));
  Register #(.width(32)) register_27 (.D(in22), .en(WE), .Q(out22), .clk(clk), .clr(reset));
  Register #(.width(32)) register_28 (.D(in30), .en(WE), .Q(out30), .clk(clk), .clr(reset));
  Register #(.width(32)) register_29 (.D(in07), .en(WE), .Q(out07), .clk(clk), .clr(reset));
  Register #(.width(32)) register_30 (.D(in15), .en(WE), .Q(out15), .clk(clk), .clr(reset));
  Register #(.width(32)) register_31 (.D(in23), .en(WE), .Q(out23), .clk(clk), .clr(reset));
  Register #(.width(32)) register_32 (.D(in31), .en(WE), .Q(out31), .clk(clk), .clr(reset));

  // Other names for the same wires on the sheet: RD1[31:0] = out_8; RD2[31:0] = out_9; WD[31:0] = in_7
endmodule

module IM (
  input  [31:0] in_1,
  output [31:0] out_2
);

  ROM #(.addrWidth(5), .dataWidth(32)) rom_1 (.addr(in_1[6:2]), .data(out_2));  // open: sel

  // Notes on the sheet:
  //   contents of rom_1 (hex, n*v repeats v):
  //   34490064 344a00fa 344b00c8 12b6021 18a6823 ac4d0004 8c4e0004 3c0f0064 11a9fffe 11cdfffd
endmodule

module NPC (
  input  [25:0] in_1,
  input  [2:0] in_2,
  input  in_3,
  input  [31:0] in_4,
  input  [31:0] in_5,
  output [31:0] out_6,
  output [31:0] PC4
);

  wire [31:0] adder_2_out, beq_bgez, bit_extender_1_out;

  Adder #(.width(32)) adder_1 (.a(in_4), .b(32'h4), .out(PC4));  // open: cin, cout
  assign bit_extender_1_out = {{14{in_1[15]}}, {in_1[15:0], 2'b00}};  // Bit_Extender bit_extender_1
  Multiplexer #(.width(32), .enable("false")) multiplexer_1 (.in0(PC4), .in1(adder_2_out), .out(beq_bgez), .sel(in_3));
  Adder #(.width(32)) adder_2 (.a(PC4), .b(bit_extender_1_out), .out(adder_2_out));  // open: cin, cout
  Multiplexer #(.select(3), .width(32)) multiplexer_2 (
    .in0(PC4), .in1(beq_bgez), .in2({in_4[31:28], in_1, 2'b00}), .in3(in_5), .out(out_6), .sel(in_2));  // open: in4, in5, in6, in7, en

  // Other names for the same wires on the sheet: cmp = in_3; imm26[25:0] = in_1; j_jal[31:2] = {in_4[31:28], in_1};
  //   PC[31:0] = in_4; jr[31:0] = in_5; NPC[31:0] = out_6; NPCsel[2:0] = in_2
endmodule

module ALU (
  input  [3:0] in_1,
  input  [4:0] in_2,
  input  [31:0] in_3,
  input  [31:0] in_4,
  output [31:0] out_5,
  output out_6
);

  wire comparator_1_eq, comparator_2_lt, comparator_3_gt, not_1_out;
  wire [31:0] _000, _001, _010, _011, _100, _101, _110, _111;

  Adder #(.width(32)) adder_1 (.a(in_3), .b(in_4), .out(_000));  // open: cin, cout
  Subtractor #(.width(32)) subtractor_1 (.a(in_3), .b(in_4), .out(_001));  // open: bin, bout
  Shifter #(.width(32)) shifter_1 (.in(in_4), .\dist (in_2), .out(_010));
  Comparator #(.width(32)) comparator_1 (.a(in_3), .b(in_4), .eq(comparator_1_eq));  // open: gt, lt
  Comparator #(.width(32)) comparator_2 (.a(in_3), .b(in_4), .lt(comparator_2_lt));  // open: gt, eq
  Comparator #(.width(32)) comparator_3 (.a(in_3), .b({32{1'b0}}), .gt(comparator_3_gt));  // open: eq, lt
  assign _110 = in_3 | in_4;  // OR_Gate or_1, 32 bits wide
  assign _111 = in_3 & in_4;  // AND_Gate and_1, 32 bits wide
  assign _011 = {{31{1'b0}}, comparator_1_eq};  // Bit_Extender bit_extender_1
  assign _100 = {{31{1'b0}}, comparator_2_lt};  // Bit_Extender bit_extender_2
  not not_1 (not_1_out, comparator_3_gt);
  assign _101 = {{31{1'b0}}, not_1_out};  // Bit_Extender bit_extender_3
  Multiplexer #(.select(4), .width(32)) multiplexer_1 (
    .in0(_000), .in1(_001), .in2(_010), .in3(_011), .in4(_100), .in5(_101), .in6(_110), .in7(_111),
    .out(out_5), .sel(in_1));  // open: in8, in9, in10, in11, in12, in13, in14, in15, en

  assign out_6 = out_5[0];

  // Other names for the same wires on the sheet: A[31:0] = in_3; B[31:0] = in_4; CTRL[3:0] = in_1; Shamt[4:0] = in_2
endmodule

module DM (
  input  in_1,
  input  in_2,
  input  in_3,
  input  [4:0] in_4,
  input  [31:0] in_5,
  output [31:0] out_6
);

  RAM #(.addrWidth(5), .dataWidth(32), .bus("separate")) ram_1 (
    .addr(in_4), .din(in_5), .data(out_6), .str(in_1), .clk(in_2), .clr(in_3));  // open: sel, ld

  // Other names for the same wires on the sheet: clk = in_2; reset = in_3; WE = in_1
endmodule

module CTR (
  input  [31:0] in_1,
  output [2:0] out_2,
  output out_3,
  output [1:0] out_4,
  output [1:0] out_5,
  output out_6,
  output [3:0] out_7,
  output out_8,
  output out_9
);

  wire addiu, addu, \and , beq, blez, comparator_10_eq, comparator_11_eq, comparator_12_eq, comparator_13_eq,
       comparator_14_eq, comparator_15_eq, j, jal, jr, lw, or_1_out, or_2_out, or_3_out, or_4_out, or_5_out,
       or_6_out, or_7_out, or_8_out, or_9_out, or_10_out, or_11_out, or_12_out, or_13_out, or_14_out, ori,
       sll, slt, special, subu, sw;

  Comparator #(.width(6), .mode("unsigned")) comparator_1 (.a(6'b100011), .b(in_1[31:26]), .eq(lw));  // open: gt, lt
  Comparator #(.width(6), .mode("unsigned")) comparator_2 (.a(6'b000100), .b(in_1[31:26]), .eq(beq));  // open: gt, lt
  buf or_1 (or_1_out, \and );  // OR_Gate
  buf or_2 (or_2_out, ori);  // OR_Gate
  buf or_3 (or_3_out, blez);  // OR_Gate
  buf or_4 (or_4_out, slt);  // OR_Gate
  buf or_5 (or_5_out, beq);  // OR_Gate
  buf or_6 (or_6_out, sll);  // OR_Gate
  buf or_7 (or_7_out, subu);  // OR_Gate
  // Priority_Encoder #(.select(4)) priority_encoder_1: pin names not known; wires that end beside it: or_7_out, or_6_out, or_5_out, or_4_out, or_3_out, or_2_out, or_1_out, out_7
  Pull_Resistor pull_resistor_1 (.node(out_7));
  Comparator #(.width(6), .mode("unsigned")) comparator_3 (.a(6'b101011), .b(in_1[31:26]), .eq(sw));  // open: gt, lt
  Comparator #(.width(6), .mode("unsigned")) comparator_4 (.a(6'b000110), .b(in_1[31:26]), .eq(blez));  // open: gt, lt
  Comparator #(.width(6), .mode("unsigned")) comparator_5 (
    .a({6{1'b0}}), .b(in_1[31:26]), .eq(special));  // open: gt, lt
  Comparator #(.width(6), .mode("unsigned")) comparator_6 (.a(6'b001101), .b(in_1[31:26]), .eq(ori));  // open: gt, lt
  Comparator #(.width(6), .mode("unsigned")) comparator_7 (.a(6'b000010), .b(in_1[31:26]), .eq(j));  // open: gt, lt
  buf or_8 (or_8_out, jr);  // OR_Gate
  or or_9 (or_9_out, j, jal);
  or or_10 (or_10_out, beq, blez);
  // Priority_Encoder #(.disabled(0)) priority_encoder_2: pin names not known; wires that end beside it: or_10_out, or_9_out, or_8_out, out_2
  Pull_Resistor pull_resistor_2 (.node(out_2));
  Comparator #(.width(6), .mode("unsigned")) comparator_8 (.a(6'b001001), .b(in_1[31:26]), .eq(addiu));  // open: gt, lt
  Comparator #(.width(6), .mode("unsigned")) comparator_9 (.a(6'b000011), .b(in_1[31:26]), .eq(jal));  // open: gt, lt
  buf or_11 (or_11_out, jal);  // OR_Gate
  or or_12 (or_12_out, lw, addiu, ori);
  Comparator #(.width(6), .mode("unsigned")) comparator_10 (
    .a(6'b100001), .b(in_1[5:0]), .eq(comparator_10_eq));  // open: gt, lt
  Comparator #(.width(6), .mode("unsigned")) comparator_11 (
    .a(6'b001000), .b(in_1[5:0]), .eq(comparator_11_eq));  // open: gt, lt
  Comparator #(.width(6), .mode("unsigned")) comparator_12 (
    .a(6'b100100), .b(in_1[5:0]), .eq(comparator_12_eq));  // open: gt, lt
  // Priority_Encoder #(.select(2)) priority_encoder_3: pin names not known; wires that end beside it: or_12_out, out_4, or_11_out
  Pull_Resistor pull_resistor_3 (.node(out_4));
  and and_1 (addu, comparator_10_eq, special);
  and and_2 (jr, comparator_11_eq, special);
  and and_3 (\and , comparator_12_eq, special);
  buf or_13 (or_13_out, jal);  // OR_Gate
  buf or_14 (or_14_out, lw);  // OR_Gate
  // Priority_Encoder #(.select(2)) priority_encoder_4: pin names not known; wires that end beside it: or_14_out, out_5, or_13_out
  Pull_Resistor pull_resistor_4 (.node(out_5));
  Comparator #(.width(6), .mode("unsigned")) comparator_13 (
    .a({6{1'b0}}), .b(in_1[5:0]), .eq(comparator_13_eq));  // open: gt, lt
  Comparator #(.width(6), .mode("unsigned")) comparator_14 (
    .a(6'b101010), .b(in_1[5:0]), .eq(comparator_14_eq));  // open: gt, lt
  Comparator #(.width(6), .mode("unsigned")) comparator_15 (
    .a(6'b100011), .b(in_1[5:0]), .eq(comparator_15_eq));  // open: gt, lt
  and and_4 (sll, comparator_13_eq, special);
  and and_5 (slt, comparator_14_eq, special);
  and and_6 (subu, comparator_15_eq, special);
  or or_15 (out_6, lw, sw, addiu);
  or or_16 (out_3, addu, sll, slt, lw, ori, jal, addiu, \and , subu);
  buf or_17 (out_9, sw);  // OR_Gate
  or or_18 (out_8, lw, sw, ori, addiu);

  // Other names for the same wires on the sheet: ALU_B_sel = out_8; ALU_op[3:0] = out_7; DM_wr = out_9;
  //   EXT_op = out_6; func[5:0] = in_1[5:0]; opcode[5:0] = in_1[31:26]; NPC_op[2:0] = out_2; RF_A3_sel[1:0] = out_4;
  //   RF_WD_sel[1:0] = out_5; RF_wr = out_3
endmodule

module EXT (
  input  in_1,
  input  [15:0] in_2,
  output [31:0] out_3
);

  wire [31:0] bit_extender_1_out, bit_extender_2_out;

  assign bit_extender_1_out = {{16{1'b0}}, in_2};  // Bit_Extender bit_extender_1
  assign bit_extender_2_out = {{16{in_2[15]}}, in_2};  // Bit_Extender bit_extender_2
  Multiplexer #(.width(32), .enable("false")) multiplexer_1 (
    .in0(bit_extender_1_out), .in1(bit_extender_2_out), .out(out_3), .sel(in_1));
endmodule

module SPLT (
  input  [31:0] in_1,
  output [25:0] out_2,
  output [15:0] out_3,
  output [4:0] out_4,
  output [4:0] out_5,
  output [4:0] out_6,
  output [4:0] out_7
);


  assign out_2 = in_1[25:0];
  assign out_3 = in_1[15:0];
  assign out_4 = in_1[25:21];
  assign out_5 = in_1[20:16];
  assign out_6 = in_1[15:11];
  assign out_7 = in_1[10:6];
endmodule
