// Logisim project add.circ as structural Verilog: 3 circuits, main circuit main
module main (
);

  cla4 cla4_1 ();  // open: cin, A, B, out, cout
endmodule

module add16 (
  input  [15:0] in_1,
  input  [15:0] in_2,
  input  in_3,
  output out_4,
  output [15:0] out_5
);

  wire cla4_1_cout, cla4_2_cout, cla4_3_cout;

  cla4 cla4_1 (.cin(in_3), .A(in_2[15:12]), .B(in_1[15:12]), .out(out_5[15:12]), .cout(cla4_1_cout));
  cla4 cla4_2 (.cin(cla4_1_cout), .A(in_2[11:8]), .B(in_1[11:8]), .out(out_5[11:8]), .cout(cla4_2_cout));
  cla4 cla4_3 (.cin(cla4_2_cout), .A(in_2[7:4]), .B(in_1[7:4]), .out(out_5[7:4]), .cout(cla4_3_cout));
  cla4 cla4_4 (.cin(cla4_3_cout), .A(in_2[3:0]), .B(in_1[3:0]), .out(out_5[3:0]), .cout(out_4));
endmodule

module cla4 (
  input  cin,
  input  [3:0] A,
  input  [3:0] B,
  output [3:0] out,
  output cout
);

  wire adder_1_cout, adder_2_cout, adder_3_cout, and_1_out, and_2_out, and_3_out, and_4_out, and_5_out,
       and_6_out, and_7_out, and_8_out, and_9_out, or_1_out, or_2_out, or_3_out, or_4_out, or_5_out,
       or_6_out, or_7_out;

  or or_1 (or_1_out, A[0], B[0]);
  and and_1 (and_1_out, A[0], B[0]);
  or or_2 (or_2_out, A[1], B[1]);
  and and_2 (and_2_out, A[1], B[1]);
  and and_3 (and_3_out, or_1_out, or_2_out, or_3_out, or_5_out);
  Adder #(.width(1)) adder_1 (.a(A[0]), .b(B[0]), .out(out[0]), .cin(cin), .cout(adder_1_cout));
  Adder #(.width(1)) adder_2 (.a(A[1]), .b(B[1]), .out(out[1]), .cin(adder_1_cout), .cout(adder_2_cout));
  Adder #(.width(1)) adder_3 (.a(A[2]), .b(B[2]), .out(out[2]), .cin(adder_2_cout), .cout(adder_3_cout));
  Adder #(.width(1)) adder_4 (.a(A[3]), .b(B[3]), .out(out[3]), .cin(adder_3_cout));  // open: cout
  and and_4 (and_4_out, and_1_out, or_2_out);
  or or_3 (or_3_out, A[2], B[2]);
  and and_5 (and_5_out, A[2], B[2]);
  or or_4 (or_4_out, and_4_out, and_2_out);
  and and_6 (and_6_out, or_4_out, or_3_out);
  or or_5 (or_5_out, A[3], B[3]);
  or or_6 (or_6_out, and_6_out, and_5_out);
  and and_7 (and_7_out, A[3], B[3]);
  and and_8 (and_8_out, or_6_out, or_5_out);
  or or_7 (or_7_out, and_8_out, and_7_out);
  and and_9 (and_9_out, cin, and_3_out);
  or or_8 (cout, or_7_out, and_9_out);
endmodule
