// Logisim project fib_easy.circ as structural Verilog: 5 circuits, main circuit main
module mul (
  input  [31:0] in_1,
  input  [31:0] in_2,
  input  [31:0] in_3,
  input  [31:0] in_4,
  input  [31:0] in_5,
  input  [31:0] in_6,
  input  [31:0] in_7,
  input  [31:0] in_8,
  output [31:0] out_9,
  output [31:0] out_10,
  output [31:0] out_11,
  output [31:0] out_12
);

  wire [31:0] multiplier_1_out, multiplier_2_out, multiplier_3_out, multiplier_4_out, multiplier_5_out,
       multiplier_6_out, multiplier_7_out, multiplier_8_out;

  Multiplier #(.width(32)) multiplier_1 (.a(in_1), .b(in_5), .out(multiplier_1_out));  // open: cin, cout
  Multiplier #(.width(32)) multiplier_2 (.a(in_2), .b(in_7), .out(multiplier_2_out));  // open: cin, cout
  Multiplier #(.width(32)) multiplier_3 (.a(in_1), .b(in_6), .out(multiplier_3_out));  // open: cin, cout
  Multiplier #(.width(32)) multiplier_4 (.a(in_2), .b(in_8), .out(multiplier_4_out));  // open: cin, cout
  Multiplier #(.width(32)) multiplier_5 (.a(in_3), .b(in_5), .out(multiplier_5_out));  // open: cin, cout
  Multiplier #(.width(32)) multiplier_6 (.a(in_4), .b(in_7), .out(multiplier_6_out));  // open: cin, cout
  Multiplier #(.width(32)) multiplier_7 (.a(in_3), .b(in_6), .out(multiplier_7_out));  // open: cin, cout
  Multiplier #(.width(32)) multiplier_8 (.a(in_4), .b(in_8), .out(multiplier_8_out));  // open: cin, cout
  Adder #(.width(32)) adder_1 (.a(multiplier_1_out), .b(multiplier_2_out), .out(out_9));  // open: cin, cout
  Adder #(.width(32)) adder_2 (.a(multiplier_3_out), .b(multiplier_4_out), .out(out_10));  // open: cin, cout
  Adder #(.width(32)) adder_3 (.a(multiplier_5_out), .b(multiplier_6_out), .out(out_11));  // open: cin, cout
  Adder #(.width(32)) adder_4 (.a(multiplier_7_out), .b(multiplier_8_out), .out(out_12));  // open: cin, cout

  // Other names for the same wires on the sheet: a1[31:0] = in_1; a2[31:0] = in_2; a3[31:0] = in_3; a4[31:0] = in_4;
  //   b1[31:0] = in_5; b2[31:0] = in_6; b3[31:0] = in_7; b4[31:0] = in_8
endmodule

module nxt (
  input  [31:0] k,
  input  [31:0] in_2,
  input  [31:0] in_3,
  input  [31:0] in_4,
  input  [31:0] in_5,
  input  [31:0] in_6,
  input  [31:0] in_7,
  input  [31:0] in_8,
  input  [31:0] in_9,
  input  jud,
  output [31:0] nk,
  output [31:0] out_12,
  output [31:0] out_13,
  output [31:0] out_14,
  output [31:0] out_15,
  output [31:0] out_16,
  output [31:0] out_17,
  output [31:0] out_18,
  output [31:0] out_19,
  output njud
);

  wire comparator_1_gt, comparator_2_gt;
  wire [31:0] and_1_out, mul_1_out_9, mul_1_out_10, mul_1_out_11, mul_1_out_12, mul_2_out_9, mul_2_out_10,
       mul_2_out_11, mul_2_out_12, mux4_1_out_10, mux4_1_out_11, mux4_1_out_12, mux4_1_out_13, shifter_1_out;

  assign and_1_out = k & 32'h1;  // AND_Gate and_1, 32 bits wide
  mul mul_1 (
    .in_1(in_2), .in_2(in_3), .in_3(in_4), .in_4(in_5), .in_5(in_6), .in_6(in_7), .in_7(in_8), .in_8(in_9),
    .out_9(mul_1_out_9), .out_10(mul_1_out_10), .out_11(mul_1_out_11), .out_12(mul_1_out_12));
  Shifter #(.width(32), .shift("lr")) shifter_1 (.in(k), .\dist (5'b00001), .out(shifter_1_out));
  Comparator #(.width(32), .mode("unsigned")) comparator_1 (
    .a(and_1_out), .b({32{1'b0}}), .gt(comparator_1_gt));  // open: eq, lt
  Multiplexer #(.width(32)) multiplexer_1 (.in0(shifter_1_out), .in1(k), .out(nk), .sel(jud));  // open: en
  not not_1 (njud, comparator_2_gt);
  Comparator #(.width(32), .mode("unsigned")) comparator_2 (
    .a(shifter_1_out), .b({32{1'b0}}), .gt(comparator_2_gt));  // open: eq, lt
  mux4 mux4_1 (
    .in_1(in_2), .in_3(in_3), .in_4(in_4), .in_5(in_5), .in_6(mul_1_out_9), .in_7(mul_1_out_10),
    .in_8(mul_1_out_11), .in_9(mul_1_out_12), .out_10(mux4_1_out_10), .out_11(mux4_1_out_11),
    .out_12(mux4_1_out_12), .out_13(mux4_1_out_13), .in_2(comparator_1_gt));
  mul mul_2 (
    .in_1(in_6), .in_2(in_7), .in_3(in_8), .in_4(in_9), .in_5(in_6), .in_6(in_7), .in_7(in_8), .in_8(in_9),
    .out_9(mul_2_out_9), .out_10(mul_2_out_10), .out_11(mul_2_out_11), .out_12(mul_2_out_12));
  mux4 mux4_2 (
    .in_1(mux4_1_out_10), .in_3(mux4_1_out_11), .in_4(mux4_1_out_12), .in_5(mux4_1_out_13), .in_6(in_2),
    .in_7(in_3), .in_8(in_4), .in_9(in_5), .out_10(out_12), .out_11(out_13), .out_12(out_14),
    .out_13(out_15), .in_2(jud));
  mux4 mux4_3 (
    .in_1(mul_2_out_9), .in_3(mul_2_out_10), .in_4(mul_2_out_11), .in_5(mul_2_out_12), .in_6(in_6),
    .in_7(in_7), .in_8(in_8), .in_9(in_9), .out_10(out_16), .out_11(out_17), .out_12(out_18),
    .out_13(out_19), .in_2(jud));

  // Other names for the same wires on the sheet: ans1[31:0] = in_2; ans2[31:0] = in_3; ans3[31:0] = in_4;
  //   ans4[31:0] = in_5; cur1[31:0] = in_6; cur2[31:0] = in_7; cur3[31:0] = in_8; cur4[31:0] = in_9;
  //   nans1[31:0] = out_12; nans2[31:0] = out_13; nans3[31:0] = out_14; nans4[31:0] = out_15; ncur1[31:0] = out_16;
  //   ncur2[31:0] = out_17; ncur3[31:0] = out_18; ncur4[31:0] = out_19
endmodule

module mux4 (
  input  [31:0] in_1,
  input  in_2,
  input  [31:0] in_3,
  input  [31:0] in_4,
  input  [31:0] in_5,
  input  [31:0] in_6,
  input  [31:0] in_7,
  input  [31:0] in_8,
  input  [31:0] in_9,
  output [31:0] out_10,
  output [31:0] out_11,
  output [31:0] out_12,
  output [31:0] out_13
);

  Multiplexer #(.width(32)) multiplexer_1 (.in0(in_1), .in1(in_6), .out(out_10), .sel(in_2));  // open: en
  Multiplexer #(.width(32)) multiplexer_2 (.in0(in_3), .in1(in_7), .out(out_11), .sel(in_2));  // open: en
  Multiplexer #(.width(32)) multiplexer_3 (.in0(in_4), .in1(in_8), .out(out_12), .sel(in_2));  // open: en
  Multiplexer #(.width(32)) multiplexer_4 (.in0(in_5), .in1(in_9), .out(out_13), .sel(in_2));  // open: en

  // Other names for the same wires on the sheet: a1[31:0] = in_1; a2[31:0] = in_3; a3[31:0] = in_4; a4[31:0] = in_5;
  //   b1[31:0] = in_6; b2[31:0] = in_7; b3[31:0] = in_8; b4[31:0] = in_9
endmodule

module main (
  input  in_1,
  input  [2:0] in_2,
  output [3:0] out_3
);

  wire clk, jud, multiplexer_1_out, nxt_1_njud, sel;
  wire [31:0] ans1, ans2, ans3, ans4, bit_extender_1_out, counter_1_q, cur1, cur2, cur3, cur4, k,
       multiplexer_2_out, mux4_1_out_10, mux4_1_out_11, mux4_1_out_12, mux4_1_out_13, mux4_2_out_10,
       mux4_2_out_11, mux4_2_out_12, mux4_2_out_13, nxt_1_nk, nxt_1_out_12, nxt_1_out_13, nxt_1_out_14,
       nxt_1_out_15, nxt_1_out_16, nxt_1_out_17, nxt_1_out_18, nxt_1_out_19, subtractor_1_out;
  wire [31:4] multiplexer_3_out;

  assign bit_extender_1_out = {{29{1'b0}}, in_2};  // Bit_Extender bit_extender_1
  Counter #(.width(32), .max('hffffffff)) counter_1 (
    .Q(counter_1_q), .clk(clk), .clr(in_1));  // open: load, D, count, carry
  Subtractor #(.width(32)) subtractor_1 (.a(bit_extender_1_out), .b(32'h1), .out(subtractor_1_out));  // open: bin, bout
  Comparator #(.width(32), .mode("unsigned")) comparator_1 (.a(counter_1_q), .b({32{1'b0}}), .gt(sel));  // open: eq, lt
  mux4 mux4_1 (
    .in_1(32'h1), .in_3({32{1'b0}}), .in_4({32{1'b0}}), .in_5(32'h1), .in_6(ans1), .in_7(ans2), .in_8(ans3),
    .in_9(ans4), .out_10(mux4_1_out_10), .out_11(mux4_1_out_11), .out_12(mux4_1_out_12),
    .out_13(mux4_1_out_13), .in_2(sel));
  mux4 mux4_2 (
    .in_1(32'h1), .in_3(32'h1), .in_4(32'h1), .in_5({32{1'b0}}), .in_6(cur1), .in_7(cur2), .in_8(cur3),
    .in_9(cur4), .out_10(mux4_2_out_10), .out_11(mux4_2_out_11), .out_12(mux4_2_out_12),
    .out_13(mux4_2_out_13), .in_2(sel));
  Multiplexer multiplexer_1 (.in0(1'b0), .in1(jud), .out(multiplexer_1_out), .sel(sel));  // open: en
  Multiplexer #(.width(32)) multiplexer_2 (
    .in0(subtractor_1_out), .in1(k), .out(multiplexer_2_out), .sel(sel));  // open: en
  Clock clock_1 (.out(clk));
  // Probe on nxt_1_nk
  nxt nxt_1 (
    .k(multiplexer_2_out), .in_2(mux4_1_out_10), .in_3(mux4_1_out_11), .in_4(mux4_1_out_12),
    .in_5(mux4_1_out_13), .in_6(mux4_2_out_10), .in_7(mux4_2_out_11), .in_8(mux4_2_out_12),
    .in_9(mux4_2_out_13), .jud(multiplexer_1_out), .nk(nxt_1_nk), .out_12(nxt_1_out_12),
    .out_13(nxt_1_out_13), .out_14(nxt_1_out_14), .out_15(nxt_1_out_15), .out_16(nxt_1_out_16),
    .out_17(nxt_1_out_17), .out_18(nxt_1_out_18), .out_19(nxt_1_out_19), .njud(nxt_1_njud));
  // Probe on nxt_1_njud
  // Probe on nxt_1_out_12
  // Probe on nxt_1_out_16
  // Probe on nxt_1_out_13
  // Probe on nxt_1_out_17
  // Probe on nxt_1_out_14
  // Probe on nxt_1_out_18
  // Probe on nxt_1_out_15
  // Probe on nxt_1_out_19
  regnew regnew_1 (
    .in_1(clk), .k(nxt_1_nk), .in_3(nxt_1_out_12), .in_4(nxt_1_out_13), .in_5(nxt_1_out_14),
    .in_6(nxt_1_out_15), .in_7(nxt_1_out_16), .in_8(nxt_1_out_17), .in_9(nxt_1_out_18), .in_10(nxt_1_out_19),
    .jud(nxt_1_njud), .nk(k), .out_14(ans1), .out_15(ans2), .out_16(ans3), .out_17(ans4), .out_18(cur1),
    .out_19(cur2), .out_20(cur3), .out_21(cur4), .njud(jud), .in_12(in_1));
  Multiplexer #(.width(32)) multiplexer_3 (
    .in0({32{1'b0}}), .in1(ans1), .out({multiplexer_3_out, out_3}), .sel(jud));  // open: en

  // Other names for the same wires on the sheet: reset = in_1
endmodule

module regnew (
  input  in_1,
  input  [31:0] k,
  input  [31:0] in_3,
  input  [31:0] in_4,
  input  [31:0] in_5,
  input  [31:0] in_6,
  input  [31:0] in_7,
  input  [31:0] in_8,
  input  [31:0] in_9,
  input  [31:0] in_10,
  input  jud,
  input  in_12,
  output [31:0] nk,
  output [31:0] out_14,
  output [31:0] out_15,
  output [31:0] out_16,
  output [31:0] out_17,
  output [31:0] out_18,
  output [31:0] out_19,
  output [31:0] out_20,
  output [31:0] out_21,
  output njud
);

  Register #(.width(32)) register_1 (.D(k), .Q(nk), .clk(in_1), .clr(in_12));  // open: en
  Register #(.width(32)) register_2 (.D(in_3), .Q(out_14), .clk(in_1), .clr(in_12));  // open: en
  Register #(.width(32)) register_3 (.D(in_4), .Q(out_15), .clk(in_1), .clr(in_12));  // open: en
  Register #(.width(32)) register_4 (.D(in_5), .Q(out_16), .clk(in_1), .clr(in_12));  // open: en
  Register #(.width(32)) register_5 (.D(in_6), .Q(out_17), .clk(in_1), .clr(in_12));  // open: en
  Register #(.width(32)) register_6 (.D(in_7), .Q(out_18), .clk(in_1), .clr(in_12));  // open: en
  Register #(.width(32)) register_7 (.D(in_8), .Q(out_19), .clk(in_1), .clr(in_12));  // open: en
  Register #(.width(32)) register_8 (.D(in_9), .Q(out_20), .clk(in_1), .clr(in_12));  // open: en
  Register #(.width(32)) register_9 (.D(in_10), .Q(out_21), .clk(in_1), .clr(in_12));  // open: en
  Register #(.width(1)) register_10 (.D(jud), .Q(njud), .clk(in_1), .clr(in_12));  // open: en
endmodule
