// Logisim project mod5.circ as structural Verilog: 2 circuits, main circuit mod5
module mod5 (
  input  In,
  input  in_2,
  output out_3,
  output out_4,
  output out_5,
  output out_6,
  output out_7
);

  wire [1:1] register_1_q, register_1_q_2;

  Register #(.width(2)) register_1 (
    .D({register_1_q[1], In}), .en(1'b1), .Q({register_1_q_2[1], register_1_q[1]}), .clk(in_2));  // open: clr
  Decoder #(.select(2), .enable("false")) decoder_1 (
    .out0(out_4), .out1(out_5), .out2(out_7), .out3(out_6), .sel({register_1_q_2[1], register_1_q[1]}));

  assign out_3 = 1'b0;
endmodule

module test (
  input  in_1,
  output out_2,
  output out_3,
  output out_4,
  output out_5,
  output out_6
);

  wire clock_1_out, rom_1_data;
  wire [3:0] counter_1_q;

  Counter #(.width(4), .max('hf)) counter_1 (
    .Q(counter_1_q), .clk(clock_1_out), .clr(in_1));  // open: load, D, count, carry
  Clock clock_1 (.out(clock_1_out));
  ROM #(.addrWidth(4), .dataWidth(1)) rom_1 (.addr(counter_1_q), .data(rom_1_data));  // open: sel
  mod5 mod5_1 (
    .In(rom_1_data), .in_2(clock_1_out), .out_3(out_2), .out_4(out_3), .out_5(out_4), .out_6(out_5),
    .out_7(out_6));

  // Notes on the sheet:
  //   contents of rom_1 (hex, n*v repeats v):
  //   0 1 0 0 1 0 0 1 0 0 1 0 0 1
endmodule
