// Logisim project source.circ as structural Verilog: 11 circuits, main circuit source
module source (
  input  in_1,
  output halt,
  output [31:0] out_3,
  output out_4,
  output [4:0] out_5,
  output [31:0] out_6,
  output out_7,
  output [4:0] out_8,
  output [31:0] out_9,
  output [31:0] out_10
);

  wire ALU_B_sel, clk, clock_1_out, cmp, comparator_1_eq;
  wire [1:0] EXT_op, RF_A3_sel, RF_WD_sel;
  wire [2:0] MR_op, MW_op, NPC_op;
  wire [3:0] ALU_op;
  wire [4:0] istr_15_11, istr_20_16, istr_25_21, Shamt;
  wire [9:0] counter_1_q;
  wire [15:0] imm16;
  wire [25:0] imm26;
  wire [31:0] ALU_C, DM_RD, EXTout, MR_Out, multiplexer_4_out, npc_1_out_6, PC4, RF_RD1, RF_RD2;

  Clock clock_1 (.out(clock_1_out));
  Counter #(.width(10), .max('h3ff), .ongoal("stay")) counter_1 (
    .Q(counter_1_q), .carry(halt), .clk(clock_1_out));  // open: load, D, count, clr
  Comparator #(.width(10), .mode("unsigned")) comparator_1 (
    .a(counter_1_q), .b(10'h180), .eq(comparator_1_eq));  // open: gt, lt
  Multiplexer multiplexer_1 (.in0(clock_1_out), .in1(1'b0), .out(clk), .sel(comparator_1_eq));  // open: en
  Register #(.width(32)) PC (.D(npc_1_out_6), .Q(out_10), .clk(clk), .clr(in_1));  // open: en
  NPC npc_1 (.out_6(npc_1_out_6), .in_4(out_10), .in_5(RF_RD1), .in_1(imm26), .in_2(NPC_op), .in_3(cmp), .PC4(PC4));
  IM im_1 (.in_1(out_10), .out_2(out_3));
  SPLT splt_1 (
    .in_1(out_3), .out_2(imm26), .out_3(imm16), .out_4(istr_25_21), .out_5(istr_20_16), .out_6(istr_15_11),
    .out_7(Shamt));
  CTR ctr_1 (
    .in_1(out_3), .out_2(NPC_op), .out_3(out_4), .out_4(RF_A3_sel), .out_5(RF_WD_sel), .out_6(EXT_op),
    .out_7(ALU_op), .out_8(ALU_B_sel), .out_9(out_7), .out_10(MW_op), .out_11(MR_op));
  EXT ext_1 (.in_2(imm16), .out_3(EXTout), .in_1(EXT_op));
  Multiplexer #(.select(2), .width(5)) multiplexer_2 (
    .in0(istr_20_16), .in1(istr_15_11), .in2({5{1'b1}}), .out(out_5), .sel(RF_A3_sel));  // open: in3, en
  RF rf_1 (
    .A1(istr_25_21), .A2(istr_20_16), .A3(out_5), .out_8(RF_RD1), .out_9(RF_RD2), .clk(clk), .WE(out_4),
    .reset(in_1), .in_7(out_6));
  Multiplexer #(.select(2), .width(32)) multiplexer_3 (
    .in0({ALU_C[31:7], out_8, ALU_C[1:0]}), .in1(MR_Out), .in2(PC4), .in3(EXTout), .out(out_6),
    .sel(RF_WD_sel));  // open: en
  Multiplexer #(.width(32)) multiplexer_4 (
    .in0(RF_RD2), .in1(EXTout), .out(multiplexer_4_out), .sel(ALU_B_sel));  // open: en
  ALU alu_1 (
    .in_3(RF_RD1), .in_4(multiplexer_4_out), .out_5({ALU_C[31:7], out_8, ALU_C[1:0]}), .in_1(ALU_op),
    .in_2(Shamt), .out_6(cmp));
  MW mw_1 (.in_3({ALU_C[31:7], out_8, ALU_C[1:0]}), .in_4(RF_RD2), .Out(out_9), .in_1(MW_op), .in_2(DM_RD));
  DM dm_1 (.in_4(out_8), .out_6(DM_RD), .in_1(out_7), .in_2(clk), .in_3(in_1), .in_5(out_9));
  MR mr_1 (.in_2({ALU_C[31:7], out_8, ALU_C[1:0]}), .in_3(DM_RD), .Out(MR_Out), .in_1(MW_op));

  // Other names for the same wires on the sheet: ALU_C[6:2] = out_8; DMaddr[4:0] = out_8; DM_wr = out_7;
  //   Istr[31:0] = out_3; MW_Out[31:0] = out_9; pc[31:0] = out_10; res = in_1; RF_WD[31:0] = out_6; RF_wr = out_4;
  //   RFaddr[4:0] = out_5

  // Notes on the sheet:
  //   CPU(mips sig_circ)
endmodule

module RF (
  input  clk,
  input  WE,
  input  reset,
  input  [4:0] A1,
  input  [4:0] A2,
  input  [4:0] A3,
  input  [31:0] in_7,
  output [31:0] out_8,
  output [31:0] out_9
);

  wire in00, in01, in02, in03, in04, in05, in06, in07, in08, in09, in10, in11, in12, in13, in14, in15, in16,
       in17, in18, in19, in20, in21, in22, in23, in24, in25, in26, in27, in28, in29, in30, in31;
  wire [31:0] out00, out01, out02, out03, out04, out05, out06, out07, out08, out09, out10, out11, out12,
       out13, out14, out15, out16, out17, out18, out19, out20, out21, out22, out23, out24, out25, out26,
       out27, out28, out29, out30, out31;

  Register #(.width(32)) register_1 (.D({32{1'b0}}), .en(in00), .Q(out00), .clk(clk), .clr(reset));
  Register #(.width(32)) register_2 (.D(in_7), .en(in08), .Q(out08), .clk(clk), .clr(reset));
  Register #(.width(32)) register_3 (.D(in_7), .en(in16), .Q(out16), .clk(clk), .clr(reset));
  Register #(.width(32)) register_4 (.D(in_7), .en(in24), .Q(out24), .clk(clk), .clr(reset));
  Demultiplexer #(.select(5), .disabled(0), .enable("false")) demultiplexer_1 (
    .out0(in00), .out1(in01), .out2(in02), .out3(in03), .out4(in04), .out5(in05), .out6(in06), .out7(in07),
    .out8(in08), .out9(in09), .out10(in10), .out11(in11), .out12(in12), .out13(in13), .out14(in14),
    .out15(in15), .out16(in16), .out17(in17), .out18(in18), .out19(in19), .out20(in20), .out21(in21),
    .out22(in22), .out23(in23), .out24(in24), .out25(in25), .out26(in26), .out27(in27), .out28(in28),
    .out29(in29), .out30(in30), .out31(in31), .in(WE), .sel(A3));
  Register #(.width(32)) register_5 (.D(in_7), .en(in01), .Q(out01), .clk(clk), .clr(reset));
  Register #(.width(32)) register_6 (.D(in_7), .en(in09), .Q(out09), .clk(clk), .clr(reset));
  Register #(.width(32)) register_7 (.D(in_7), .en(in17), .Q(out17), .clk(clk), .clr(reset));
  Register #(.width(32)) register_8 (.D(in_7), .en(in25), .Q(out25), .clk(clk), .clr(reset));
  Register #(.width(32)) register_9 (.D(in_7), .en(in02), .Q(out02), .clk(clk), .clr(reset));
  Register #(.width(32)) register_10 (.D(in_7), .en(in10), .Q(out10), .clk(clk), .clr(reset));
  Register #(.width(32)) register_11 (.D(in_7), .en(in18), .Q(out18), .clk(clk), .clr(reset));
  Register #(.width(32)) register_12 (.D(in_7), .en(in26), .Q(out26), .clk(clk), .clr(reset));
  Register #(.width(32)) register_13 (.D(in_7), .en(in03), .Q(out03), .clk(clk), .clr(reset));
  Register #(.width(32)) register_14 (.D(in_7), .en(in11), .Q(out11), .clk(clk), .clr(reset));
  Register #(.width(32)) register_15 (.D(in_7), .en(in19), .Q(out19), .clk(clk), .clr(reset));
  Register #(.width(32)) register_16 (.D(in_7), .en(in27), .Q(out27), .clk(clk), .clr(reset));
  Multiplexer #(.select(5), .width(32), .enable("false")) multiplexer_1 (
    .in0(out00), .in1(out01), .in2(out02), .in3(out03), .in4(out04), .in5(out05), .in6(out06), .in7(out07),
    .in8(out08), .in9(out09), .in10(out10), .in11(out11), .in12(out12), .in13(out13), .in14(out14),
    .in15(out15), .in16(out16), .in17(out17), .in18(out18), .in19(out19), .in20(out20), .in21(out21),
    .in22(out22), .in23(out23), .in24(out24), .in25(out25), .in26(out26), .in27(out27), .in28(out28),
    .in29(out29), .in30(out30), .in31(out31), .out(out_8), .sel(A1));
  Register #(.width(32)) register_17 (.D(in_7), .en(in04), .Q(out04), .clk(clk), .clr(reset));
  Register #(.width(32)) register_18 (.D(in_7), .en(in12), .Q(out12), .clk(clk), .clr(reset));
  Register #(.width(32)) register_19 (.D(in_7), .en(in20), .Q(out20), .clk(clk), .clr(reset));
  Register #(.width(32)) register_20 (.D(in_7), .en(in28), .Q(out28), .clk(clk), .clr(reset));
  Register #(.width(32)) register_21 (.D(in_7), .en(in05), .Q(out05), .clk(clk), .clr(reset));
  Register #(.width(32)) register_22 (.D(in_7), .en(in13), .Q(out13), .clk(clk), .clr(reset));
  Register #(.width(32)) register_23 (.D(in_7), .en(in21), .Q(out21), .clk(clk), .clr(reset));
  Register #(.width(32)) register_24 (.D(in_7), .en(in29), .Q(out29), .clk(clk), .clr(reset));
  Multiplexer #(.select(5), .width(32), .enable("false")) multiplexer_2 (
    .in0(out00), .in1(out01), .in2(out02), .in3(out03), .in4(out04), .in5(out05), .in6(out06), .in7(out07),
    .in8(out08), .in9(out09), .in10(out10), .in11(out11), .in12(out12), .in13(out13), .in14(out14),
    .in15(out15), .in16(out16), .in17(out17), .in18(out18), .in19(out19), .in20(out20), .in21(out21),
    .in22(out22), .in23(out23), .in24(out24), .in25(out25), .in26(out26), .in27(out27), .in28(out28),
    .in29(out29), .in30(out30), .in31(out31), .out(out_9), .sel(A2));
  Register #(.width(32)) register_25 (.D(in_7), .en(in06), .Q(out06), .clk(clk), .clr(reset));
  Register #(.width(32)) register_26 (.D(in_7), .en(in14), .Q(out14), .clk(clk), .clr(reset));
  Register #(.width(32)) register_27 (.D(in_7), .en(in22), .Q(out22), .clk(clk), .clr(reset));
  Register #(.width(32)) register_28 (.D(in_7), .en(in30), .Q(out30), .clk(clk), .clr(reset));
  Register #(.width(32)) register_29 (.D(in_7), .en(in07), .Q(out07), .clk(clk), .clr(reset));
  Register #(.width(32)) register_30 (.D(in_7), .en(in15), .Q(out15), .clk(clk), .clr(reset));
  Register #(.width(32)) register_31 (.D(in_7), .en(in23), .Q(out23), .clk(clk), .clr(reset));
  Register #(.width(32)) register_32 (.D(in_7), .en(in31), .Q(out31), .clk(clk), .clr(reset));

  // Other names for the same wires on the sheet: RD1[31:0] = out_8; RD2[31:0] = out_9; WD[31:0] = in_7
endmodule

module IM (
  input  [31:0] in_1,
  output [31:0] out_2
);

  ROM #(.addrWidth(10), .dataWidth(32)) rom_1 (.addr(in_1[11:2]), .data(out_2));  // open: sel

  // Notes on the sheet:
  //   contents of rom_1 (hex, n*v repeats v):
  //   03fff823 8c040020 03e31821 34204ac0 00000000 007e282a 00000000 001e0824 8c1f003c 03e3f82a 3c019a4e
  //   24444f93 3c1e3e1d 343fa868 00a01821 8c05000c 8c02000c 246151fe ac020010 00a02824 00251823 00000000
  //   00000000 ac01001c 37e46a4f 8c050024 3c1fb426 0064102a 3c047cde 00810021 347f29f3 00000000 00000000
  //   009e1024 03c3202a 00000000 03c4002a 009ff024 00a42824 0061f024 8c1e0034 03e21023 3c1f7e80 ac02006c
  //   ac030030 37c527d1 03ff1823 00000000 3c05f32a 3c027ce1 00a4f821 00431821 3c047cd1 0004102a 00000000
  //   00032f00 00000000 3c05a384 3c00af1e 00000000 241e271d 8c1f0000 3c025326 00000000 24bf5b2f 00000000
  //   34a29ce8 00012280 00000000 00250821 0023f024 0005f824 0082202a ac040000 00a4f823 344294e4 009f082a
  //   34a08d53 ac050024 00000000 00000000 00220021 001ff300 8c1e0030 340368d0 00002c40 009e282a 00000000
  //   0062002a 00000000 00000000 00231821 0800008a 03c40821 0c00006c 8c050018 3c01319c 37e0ea11 27e03473
  //   003ff021 0c000094 8c1e0054 0c000077 00000000 0c00006c 00811023 0023f823 0c000070 34635c33 3c052d62
  //   00232021 00020500 00201021 0064102a 107f0021 03c42823 10000015 00000000 10450017 00012440 8c010034
  //   ac000024 3c1fe200 341e8538 00000000 00400823 03e42824 ac00004c 000221c0 00000000 00000000 00a3282a
  //   00000000 0c000098 3c05b07a 13fe0023 0022182a 0044002a 8c1e0008 00000000 00000000 1040001d 00202023
  //   10610014 3c056da4 03de2823 3440930e 8c00001c 0c0000c0 00000000 107f0014 00000000 0064f823 34642f64
  //   0062002a 24805e43 1025001c 00830023 03e2f02a 080000c4 240122e1 8c1f0050 000213c0 101f0004 3c032bc7
  //   080000bd 3c01a1b4 03e40823 8c1f0020 00000000 00a52021 00000000 03df2024 34847a95 1000000d 8c020054
  //   3442b939 ac000020 13e50004 0003f040 005f0824 3c04422f 343e81f3 ac030038 00000000 00000000 00a4f024
  //   00621824 0085082a 2402589e 0000f023 24247adf 0c0000e8 00050a80 001ff300 13e30001 00421824 24033249
  //   8c050058 3c03d919 1002001f 3c04768e 24456abd 00a1f024 1025000c 00a02824 03e01023 8c050008 00000000
  //   ac00002c 34a12635 3425c20d 03e1102a 00441823 0082f821 246301f5 00000000 0c0000f5 00000000 00212024
  //   080000fe ac050004 00000000 3c02278d 8c1f0054 00000000 109e0010 005e102a 00000000 00202824 ac03001c
  //   3c006e03 00450823 248265fe 080000ec 3c01eacf 080000f5 00bf0024 00000000 00000000 8c020074 349e76dd
  //   13c10011 0000f024 03c10023 03ff182a 24a4163b 8c00003c 00be2824 8c1f0054 00000000 08000101 00000000
  //   37e267b2 ac040030 08000129 8c03001c 1084001e 00000000 109e000c 8c1f0078 0021f821 00000000 346578ae
  //   3c1f6a0c 10600011 00000000 248466f7 03fe0023 13de0031 00000000 08000135 00000000 0c000122 00000000
  //   0001f000 00000000 ac020018 03fff823 0020182a 0c000122 8c050054 03e2f021 ac010048 24453eea 0800014b
  //   3c1fe974 00000000 00000000 0c00013c 00000000 10630014 03c52024 00000000 105e000b 8c040078 00211024
  //   1083001e ac1e0024 10be0027 00022823 03ff2821 ac05003c 03ff082a 00000000 341e7c47 00022600 00051940
  //   00000000 1021002b 001e2a80 00432824 0023202a 00032c80 ac020070 0c00016c 03def821 005f0821 00a30024
  //   27c156d0 00020824 00000000 00a5282a 00000000 00000000 03c42023 0001fb00 00000000 00011021 00000000
  //   08000155 00000000 0045f821 0c000157 009e1824 0024202a 00421823 ac030058 0040f824 ac02003c 00001b00
  //   0c000164 03c01024 00000000 3c0493cb 0800015e 3483a289 007f102a 00840823 3c1e7de2 37c251b9 00650823
  //   00000000 00420821 0020102a 00202021 00000000 8c1f0000 0024f824 ac1e0044 00000000 001ffec0 10820019
  //   0000282a 3c05b205 8c02002c 00601023 3c1e8cb2 00841024 3c04ae4a 00000000 00002c80 8c040074 00000000
  //   10bf0009 3c1ea842 37c043e8 00000000 00000000 00042823 00a3f823 24a231fd 00000000 34a3bef5 00000000
  //   0c000188 03ff2823 3c1e6ddb 10a50023 3c1e2b8d 00a0f82a 10440017 3c1f81f0 00851024 00000000 3c1fa302
  //   03e20823 8c030008 3c1e7569 34029be7 00000000 3c1f7b63 003f002a 03c0f82a 00001080 00030380 00000000
  //   080001bc 00000000 00231823 00022ac0 080001b1 00a20023 8c030040 00400024 003ef82a 0c0001ad 00601824
  //   003e1824 27c45f14 0062f024 3c028938 00000000 0c0001b0 00000000 080001ba 00820824 24645a47 0c0001c1
  //   03ff1021 8c000040 00000000 00201824 10a0002a 001ef080 00000000 1003000e 00841821 ac000004 080001be
  //   24be1362 13e10018 8c020020 ac02001c 37c0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
endmodule

module NPC (
  input  [25:0] in_1,
  input  [2:0] in_2,
  input  in_3,
  input  [31:0] in_4,
  input  [31:0] in_5,
  output [31:0] out_6,
  output [31:0] PC4
);

  wire [31:0] adder_2_out, beq_bgez, bit_extender_1_out;

  Adder #(.width(32)) adder_1 (.a(in_4), .b(32'h4), .out(PC4));  // open: cin, cout
  assign bit_extender_1_out = {{14{in_1[15]}}, {in_1[15:0], 2'b00}};  // Bit_Extender bit_extender_1
  Multiplexer #(.width(32), .enable("false")) multiplexer_1 (.in0(PC4), .in1(adder_2_out), .out(beq_bgez), .sel(in_3));
  Adder #(.width(32)) adder_2 (.a(PC4), .b(bit_extender_1_out), .out(adder_2_out));  // open: cin, cout
  Multiplexer #(.select(3), .width(32)) multiplexer_2 (
    .in0(PC4), .in1(beq_bgez), .in2({in_4[31:28], in_1, 2'b00}), .in3(in_5), .out(out_6), .sel(in_2));  // open: in4, in5, in6, in7, en

  // Other names for the same wires on the sheet: cmp = in_3; imm26[25:0] = in_1; j_jal[31:2] = {in_4[31:28], in_1};
  //   PC[31:0] = in_4; jr[31:0] = in_5; NPC[31:0] = out_6; NPCsel[2:0] = in_2
endmodule

module ALU (
  input  [3:0] in_1,
  input  [4:0] in_2,
  input  [31:0] in_3,
  input  [31:0] in_4,
  output [31:0] out_5,
  output out_6
);

  wire comparator_1_eq, comparator_2_lt, comparator_3_gt, not_1_out;
  wire [31:0] _000, _001, _010, _011, _100, _101, _110, _111;

  Adder #(.width(32)) adder_1 (.a(in_3), .b(in_4), .out(_000));  // open: cin, cout
  Subtractor #(.width(32)) subtractor_1 (.a(in_3), .b(in_4), .out(_001));  // open: bin, bout
  Shifter #(.width(32)) shifter_1 (.in(in_4), .\dist (in_2), .out(_010));
  Comparator #(.width(32)) comparator_1 (.a(in_3), .b(in_4), .eq(comparator_1_eq));  // open: gt, lt
  Comparator #(.width(32)) comparator_2 (.a(in_3), .b(in_4), .lt(comparator_2_lt));  // open: gt, eq
  Comparator #(.width(32)) comparator_3 (.a(in_3), .b({32{1'b0}}), .gt(comparator_3_gt));  // open: eq, lt
  assign _110 = in_3 | in_4;  // OR_Gate or_1, 32 bits wide
  assign _111 = in_3 & in_4;  // AND_Gate and_1, 32 bits wide
  assign _011 = {{31{1'b0}}, comparator_1_eq};  // Bit_Extender bit_extender_1
  assign _100 = {{31{1'b0}}, comparator_2_lt};  // Bit_Extender bit_extender_2
  assign _101 = {{31{1'b0}}, not_1_out};  // Bit_Extender bit_extender_3
  not not_1 (not_1_out, comparator_3_gt);
  Multiplexer #(.select(4), .width(32)) multiplexer_1 (
    .in0(_000), .in1(_001), .in2(_010), .in3(_011), .in4(_100), .in5(_101), .in6(_110), .in7(_111),
    .in15({32{1'b0}}), .out(out_5), .sel(in_1));  // open: in8, in9, in10, in11, in12, in13, in14, en

  assign out_6 = out_5[0];

  // Other names for the same wires on the sheet: A[31:0] = in_3; B[31:0] = in_4; CTRL[3:0] = in_1; Shamt[4:0] = in_2
endmodule

module DM (
  input  in_1,
  input  in_2,
  input  in_3,
  input  [4:0] in_4,
  input  [31:0] in_5,
  output [31:0] out_6
);

  RAM #(.addrWidth(5), .dataWidth(32), .bus("separate")) ram_1 (
    .addr(in_4), .din(in_5), .data(out_6), .str(in_1), .clk(in_2), .clr(in_3));  // open: sel, ld

  // Other names for the same wires on the sheet: clk = in_2; reset = in_3; WE = in_1
endmodule

module CTR (
  input  [31:0] in_1,
  output [2:0] out_2,
  output out_3,
  output [1:0] out_4,
  output [1:0] out_5,
  output [1:0] out_6,
  output [3:0] out_7,
  output out_8,
  output out_9,
  output [2:0] out_10,
  output [2:0] out_11
);

  wire addiu, addu, \and , beq, blez, comparator_13_eq, comparator_14_eq, comparator_15_eq, comparator_16_eq,
       comparator_17_eq, comparator_18_eq, j, jal, jr, lb, lui, lw, or_1_out, or_2_out, or_3_out, or_4_out,
       or_5_out, or_6_out, or_7_out, or_9_out, or_10_out, or_11_out, or_12_out, or_13_out, or_14_out,
       or_15_out, or_16_out, ori, priority_encoder_1_p9, sb, sll, slt, special, subu, sw;

  Comparator #(.width(6), .mode("unsigned")) comparator_1 (.a(6'b100011), .b(in_1[31:26]), .eq(lw));  // open: gt, lt
  Comparator #(.width(6), .mode("unsigned")) comparator_2 (.a(6'b000100), .b(in_1[31:26]), .eq(beq));  // open: gt, lt
  buf or_1 (or_1_out, \and );  // OR_Gate
  buf or_2 (or_2_out, ori);  // OR_Gate
  buf or_3 (or_3_out, blez);  // OR_Gate
  buf or_4 (or_4_out, slt);  // OR_Gate
  buf or_5 (or_5_out, beq);  // OR_Gate
  buf or_6 (or_6_out, sll);  // OR_Gate
  buf or_7 (or_7_out, subu);  // OR_Gate
  // Priority_Encoder #(.select(4)) priority_encoder_1: pin names not known; wires that end beside it: or_7_out, or_6_out, or_5_out, or_4_out, or_3_out, or_2_out, or_1_out, out_7, priority_encoder_1_p9
  Pull_Resistor pull_resistor_1 (.node(out_7));
  Comparator #(.width(6), .mode("unsigned")) comparator_3 (.a(6'b101011), .b(in_1[31:26]), .eq(sw));  // open: gt, lt
  Comparator #(.width(6), .mode("unsigned")) comparator_4 (.a(6'b000110), .b(in_1[31:26]), .eq(blez));  // open: gt, lt
  Comparator #(.width(6), .mode("unsigned")) comparator_5 (.a(6'b001111), .b(in_1[31:26]), .eq(lui));  // open: gt, lt
  buf or_8 (priority_encoder_1_p9, lui);  // OR_Gate
  buf or_9 (or_9_out, jr);  // OR_Gate
  or or_10 (or_10_out, j, jal);
  or or_11 (or_11_out, beq, blez);
  Comparator #(.width(6), .mode("unsigned")) comparator_6 (
    .a({6{1'b0}}), .b(in_1[31:26]), .eq(special));  // open: gt, lt
  Comparator #(.width(6), .mode("unsigned")) comparator_7 (.a(6'b001101), .b(in_1[31:26]), .eq(ori));  // open: gt, lt
  Comparator #(.width(6), .mode("unsigned")) comparator_8 (.a(6'b000010), .b(in_1[31:26]), .eq(j));  // open: gt, lt
  Comparator #(.width(6), .mode("unsigned")) comparator_9 (.a(6'b100000), .b(in_1[31:26]), .eq(lb));  // open: gt, lt
  // Priority_Encoder #(.disabled(0)) priority_encoder_2: pin names not known; wires that end beside it: or_11_out, or_10_out, or_9_out, out_2
  Pull_Resistor pull_resistor_2 (.node(out_2));
  Comparator #(.width(6), .mode("unsigned")) comparator_10 (
    .a(6'b001001), .b(in_1[31:26]), .eq(addiu));  // open: gt, lt
  Comparator #(.width(6), .mode("unsigned")) comparator_11 (.a(6'b000011), .b(in_1[31:26]), .eq(jal));  // open: gt, lt
  Comparator #(.width(6), .mode("unsigned")) comparator_12 (.a(6'b101000), .b(in_1[31:26]), .eq(sb));  // open: gt, lt
  buf or_12 (or_12_out, jal);  // OR_Gate
  // Priority_Encoder #(.select(2)) priority_encoder_3: pin names not known; wires that end beside it: special, out_4, or_12_out
  Pull_Resistor pull_resistor_3 (.node(out_4));
  Comparator #(.width(6), .mode("unsigned")) comparator_13 (
    .a(6'b100001), .b(in_1[5:0]), .eq(comparator_13_eq));  // open: gt, lt
  Comparator #(.width(6), .mode("unsigned")) comparator_14 (
    .a(6'b001000), .b(in_1[5:0]), .eq(comparator_14_eq));  // open: gt, lt
  Comparator #(.width(6), .mode("unsigned")) comparator_15 (
    .a(6'b100100), .b(in_1[5:0]), .eq(comparator_15_eq));  // open: gt, lt
  buf or_13 (or_13_out, lui);  // OR_Gate
  or or_14 (or_14_out, lw, sw, sb, lb, addiu);
  // Priority_Encoder #(.select(2)) priority_encoder_4: pin names not known; wires that end beside it: or_14_out, out_6, or_13_out
  Pull_Resistor pull_resistor_4 (.node(out_6));
  buf or_15 (or_15_out, jal);  // OR_Gate
  or or_16 (or_16_out, lw, lb);
  // Priority_Encoder #(.select(2)) priority_encoder_5: pin names not known; wires that end beside it: or_16_out, out_5, or_15_out, lui
  Pull_Resistor pull_resistor_5 (.node(out_5));
  and and_1 (addu, comparator_13_eq, special);
  and and_2 (jr, comparator_14_eq, special);
  and and_3 (\and , comparator_15_eq, special);
  Comparator #(.width(6), .mode("unsigned")) comparator_16 (
    .a({6{1'b0}}), .b(in_1[5:0]), .eq(comparator_16_eq));  // open: gt, lt
  Comparator #(.width(6), .mode("unsigned")) comparator_17 (
    .a(6'b101010), .b(in_1[5:0]), .eq(comparator_17_eq));  // open: gt, lt
  Comparator #(.width(6), .mode("unsigned")) comparator_18 (
    .a(6'b100011), .b(in_1[5:0]), .eq(comparator_18_eq));  // open: gt, lt
  // Priority_Encoder #(.disabled(0)) priority_encoder_6: pin names not known; wires that end beside it: lb, out_11
  Pull_Resistor pull_resistor_6 (.node(out_11));
  // Priority_Encoder #(.disabled(0)) priority_encoder_7: pin names not known; wires that end beside it: sb, out_10
  Pull_Resistor pull_resistor_7 (.node(out_10));
  and and_4 (sll, comparator_16_eq, special);
  and and_5 (slt, comparator_17_eq, special);
  and and_6 (subu, comparator_18_eq, special);
  or or_17 (out_3, lb, addu, sll, slt, lw, ori, jal, addiu, \and , subu, lui);
  or or_18 (out_9, sb, sw);
  or or_19 (out_8, lw, sw, ori, addiu, lb, sb);

  // Other names for the same wires on the sheet: ALU_B_sel = out_8; ALU_op[3:0] = out_7; DM_wr = out_9;
  //   EXT_op[1:0] = out_6; func[5:0] = in_1[5:0]; opcode[5:0] = in_1[31:26]; MR_op[2:0] = out_11; MW_op[2:0] = out_10;
  //   NPC_op[2:0] = out_2; RF_A3_sel[1:0] = out_4; RF_WD_sel[1:0] = out_5; RF_wr = out_3
endmodule

module EXT (
  input  [1:0] in_1,
  input  [15:0] in_2,
  output [31:0] out_3
);

  wire [31:0] bit_extender_1_out, bit_extender_2_out;

  assign bit_extender_1_out = {{16{1'b0}}, in_2};  // Bit_Extender bit_extender_1
  assign bit_extender_2_out = {{16{in_2[15]}}, in_2};  // Bit_Extender bit_extender_2
  Multiplexer #(.select(2), .width(32), .enable("false")) multiplexer_1 (
    .in0(bit_extender_1_out), .in1(bit_extender_2_out), .in2({in_2, {16{1'b0}}}), .out(out_3), .sel(in_1));  // open: in3
endmodule

module SPLT (
  input  [31:0] in_1,
  output [25:0] out_2,
  output [15:0] out_3,
  output [4:0] out_4,
  output [4:0] out_5,
  output [4:0] out_6,
  output [4:0] out_7
);


  assign out_2 = in_1[25:0];
  assign out_3 = in_1[15:0];
  assign out_4 = in_1[25:21];
  assign out_5 = in_1[20:16];
  assign out_6 = in_1[15:11];
  assign out_7 = in_1[10:6];
endmodule

module MW (
  input  [2:0] in_1,
  input  [31:0] in_2,
  input  [31:0] in_3,
  input  [31:0] in_4,
  output [31:0] Out
);

  wire [31:0] sb;

  Multiplexer #(.select(2), .width(32)) multiplexer_1 (
    .in0({in_2[31:8], in_4[7:0]}), .in1({in_2[31:16], in_4[7:0], in_2[7:0]}),
    .in2({in_2[31:24], in_4[7:0], in_2[15:0]}), .in3({in_4[7:0], in_2[23:0]}), .out(sb), .sel(in_3[1:0]));  // open: en
  Multiplexer #(.select(3), .width(32)) multiplexer_2 (
    .in0(in_4), .in1(sb), .out(Out), .sel(in_1));  // open: in2, in3, in4, in5, in6, in7, en

  // Other names for the same wires on the sheet: _00[31:0] = {in_2[31:8], in_4[7:0]};
  //   _01[31:0] = {in_2[31:16], in_4[7:0], in_2[7:0]}; _11[31:0] = {in_4[7:0], in_2[23:0]}; Mem[31:0] = in_2;
  //   _10[31:0] = {in_2[31:24], in_4[7:0], in_2[15:0]}; sw[31:0] = in_4; WD[31:0] = in_4; A[31:0] = in_3;
  //   byte[1:0] = in_3[1:0]; MW_op[2:0] = in_1
endmodule

module MR (
  input  [2:0] in_1,
  input  [31:0] in_2,
  input  [31:0] in_3,
  output [31:0] Out
);

  wire [31:0] _00, _01, _10, _11, lb;

  assign _00 = {{24{in_3[7]}}, in_3[7:0]};  // Bit_Extender bit_extender_1
  assign _01 = {{24{in_3[15]}}, in_3[15:8]};  // Bit_Extender bit_extender_2
  assign _10 = {{24{in_3[23]}}, in_3[23:16]};  // Bit_Extender bit_extender_3
  assign _11 = {{24{in_3[31]}}, in_3[31:24]};  // Bit_Extender bit_extender_4
  Multiplexer #(.select(2), .width(32)) multiplexer_1 (
    .in0(_00), .in1(_01), .in2(_10), .in3(_11), .out(lb), .sel(in_2[1:0]));  // open: en
  Multiplexer #(.select(3), .width(32)) multiplexer_2 (
    .in0(in_3), .in1(lb), .out(Out), .sel(in_1));  // open: in2, in3, in4, in5, in6, in7, en

  // Other names for the same wires on the sheet: A[31:0] = in_2; byte[1:0] = in_2[1:0]; lw[31:0] = in_3;
  //   Mem[31:0] = in_3; MR_op[2:0] = in_1
endmodule
