// Logisim project std.circ as structural Verilog: 11 circuits, main circuit main
module main (
  input  rst,
  output halt,
  output [31:0] out_3,
  output RFWr,
  output [4:0] out_5,
  output [31:0] out_6,
  output out_7,
  output [4:0] out_8,
  output [31:0] out_9,
  output [31:0] out_10
);

  wire ALUZero, BSel, clk, clock_1_out, comparator_1_eq, EXTOp;
  wire [1:0] A3Sel, WDSel;
  wire [2:0] Br, DMType;
  wire [3:0] cu_1_alucontrol;
  wire [4:0] shamt, splt_1__11_15, splt_1__16_20, splt_1__21_25;
  wire [7:0] counter_1_q;
  wire [15:0] splt_1__0_15;
  wire [25:0] imm26;
  wire [31:0] ALUout, DMout, DMtemp, EXTout, multiplexer_4_out, mw_1_out_5, npc_1_out_6, PC4, RD1;

  Counter #(.max('h1f), .ongoal("stay")) counter_1 (
    .Q(counter_1_q), .carry(halt), .clk(clock_1_out));  // open: load, D, count, clr
  Clock clock_1 (.out(clock_1_out));
  Comparator #(.mode("unsigned")) comparator_1 (.a(counter_1_q), .b(8'h1f), .eq(comparator_1_eq));  // open: gt, lt
  Multiplexer multiplexer_1 (.in0(clock_1_out), .in1(1'b0), .out(clk), .sel(comparator_1_eq));  // open: en
  IM IM (.addr(out_10), .RD(out_3));
  Register #(.width(32)) PC (.D(npc_1_out_6), .Q(out_10), .clk(clk), .clr(rst));  // open: en
  NPC npc_1 (.out_6(npc_1_out_6), .IMM26(imm26), .RA(RD1), .PC(out_10), .Br(Br), .ALUZero(ALUZero), .PC4(PC4));
  CU cu_1 (
    .in_1(out_3), .Br(Br), .A3Sel(A3Sel), .WDSel(WDSel), .RFWr(RFWr), .EXTOp(EXTOp), .DMWr(out_7),
    .BSel(BSel), .DMType(DMType), .ALUControl(cu_1_alucontrol));
  SPLT splt_1 (
    .instr(out_3), ._0_25(imm26), ._21_25(splt_1__21_25), ._16_20(splt_1__16_20), ._11_15(splt_1__11_15),
    ._0_15(splt_1__0_15), ._6_10(shamt));
  EXT ext_1 (.in_1(splt_1__0_15), .\signed (EXTOp), .out(EXTout));
  Multiplexer #(.select(2), .width(5)) multiplexer_2 (
    .in0(splt_1__16_20), .in1(splt_1__11_15), .in2({5{1'b1}}), .out(out_5), .sel(A3Sel));  // open: in3, en
  Multiplexer #(.select(2), .width(32)) multiplexer_3 (
    .in0({ALUout[31:7], out_8, ALUout[1:0]}), .in1(DMout), .in2(PC4), .out(out_6), .sel(WDSel));  // open: in3, en
  GRF RF (
    .A1(splt_1__21_25), .A2(splt_1__16_20), .A3(out_5), .WD(out_6), .RD1(RD1), .RD2(out_9), .we(RFWr),
    .rst(rst), .in_1(clk));
  Multiplexer #(.width(32)) multiplexer_4 (.in0(out_9), .in1(EXTout), .out(multiplexer_4_out), .sel(BSel));  // open: en
  ALU ALU (
    .SrcA(RD1), .SrcB(multiplexer_4_out), .zero(ALUZero), .ALUControl(cu_1_alucontrol),
    .Result({ALUout[31:7], out_8, ALUout[1:0]}), .shamt(shamt));
  MW mw_1 (
    .ALUdata(out_9), .oldData(DMtemp), .addr({ALUout[31:7], out_8, ALUout[1:0]}), .\type (DMType),
    .out_5(mw_1_out_5));
  DM dm_1 (.WD(mw_1_out_5), .RD(DMtemp), .we(out_7), .rst(rst), .A(out_8), .in_4(clk));
  MR mr_1 (.data(DMtemp), .addr({ALUout[31:7], out_8, ALUout[1:0]}), .\type (DMType), .out_4(DMout));

  // Other names for the same wires on the sheet: ALUout[6:2] = out_8; MemAddr[4:0] = out_8; DMWr = out_7;
  //   Instr[31:0] = out_3; pc[31:0] = out_10; RD2[31:0] = out_9; regAddr[4:0] = out_5; regData[31:0] = out_6

  // Notes on the sheet:
  //   25:0
  //   25:21
  //   20:16
  //   15:11
  //   15:0/imm
endmodule

module IM (
  input  [31:0] addr,
  output [31:0] RD
);

  ROM #(.addrWidth(5), .dataWidth(32)) rom_1 (.addr(addr[6:2]), .data(RD));  // open: sel

  // Notes on the sheet:
  //   contents of rom_1 (hex, n*v repeats v):
  //   03fff823 3c02bed7 00021821 00400021 00631823 8c1f0060 03e21021 8c010068 346355dc 3440436f 3c1fab5c
  //   13e10000 34629bab ac000014 00000000 ac000070 08000012 8c030028 105f0001 ac1f005c 10010002 00000000
  //   8c1f002c 10410003 3c03da6b 0800001c ac03005c ac020034 00610023 ac000040 00410023 03ff1823
endmodule

module SPLT (
  input  [31:0] instr,
  output [25:0] _0_25,
  output [4:0] _21_25,
  output [4:0] _16_20,
  output [4:0] _11_15,
  output [15:0] _0_15,
  output [4:0] _6_10
);


  assign _0_15 = instr[15:0];
  assign _0_25 = instr[25:0];
  assign _6_10 = instr[10:6];
  assign _11_15 = instr[15:11];
  assign _16_20 = instr[20:16];
  assign _21_25 = instr[25:21];
endmodule

module GRF (
  input  in_1,
  input  we,
  input  [4:0] A1,
  input  [4:0] A2,
  input  [4:0] A3,
  input  [31:0] WD,
  input  rst,
  output [31:0] RD1,
  output [31:0] RD2
);

  wire [31:0] i0, i1, i2, i3, i4, i5, i6, i7, i8, i9, i10, i11, i12, i13, i14, i15, i16, i17, i18, i19, i20,
       i21, i22, i23, i24, i25, i26, i27, i28, i29, i30, i31, o0, o1, o2, o3, o4, o5, o6, o7, o8, o9, o10,
       o11, o12, o13, o14, o15, o16, o17, o18, o19, o20, o21, o22, o23, o24, o25, o26, o27, o28, o29, o30,
       o31;

  Register #(.width(32)) r0 (.D({32{1'b0}}), .en(we), .Q(o0), .clk(in_1), .clr(rst));
  Register #(.width(32)) r1 (.D(i1), .en(we), .Q(o1), .clk(in_1), .clr(rst));
  Register #(.width(32)) r2 (.D(i2), .en(we), .Q(o2), .clk(in_1), .clr(rst));
  Register #(.width(32)) r3 (.D(i3), .en(we), .Q(o3), .clk(in_1), .clr(rst));
  Register #(.width(32)) r4 (.D(i4), .en(we), .Q(o4), .clk(in_1), .clr(rst));
  Register #(.width(32)) r5 (.D(i5), .en(we), .Q(o5), .clk(in_1), .clr(rst));
  Register #(.width(32)) r6 (.D(i6), .en(we), .Q(o6), .clk(in_1), .clr(rst));
  Register #(.width(32)) r7 (.D(i7), .en(we), .Q(o7), .clk(in_1), .clr(rst));
  Register #(.width(32)) r8 (.D(i8), .en(we), .Q(o8), .clk(in_1), .clr(rst));
  Register #(.width(32)) r9 (.D(i9), .en(we), .Q(o9), .clk(in_1), .clr(rst));
  Register #(.width(32)) r10 (.D(i10), .en(we), .Q(o10), .clk(in_1), .clr(rst));
  Register #(.width(32)) r11 (.D(i11), .en(we), .Q(o11), .clk(in_1), .clr(rst));
  Register #(.width(32)) r12 (.D(i12), .en(we), .Q(o12), .clk(in_1), .clr(rst));
  Register #(.width(32)) r13 (.D(i13), .en(we), .Q(o13), .clk(in_1), .clr(rst));
  Register #(.width(32)) r14 (.D(i14), .en(we), .Q(o14), .clk(in_1), .clr(rst));
  Register #(.width(32)) r15 (.D(i15), .en(we), .Q(o15), .clk(in_1), .clr(rst));
  Register #(.width(32)) r16 (.D(i16), .en(we), .Q(o16), .clk(in_1), .clr(rst));
  Register #(.width(32)) r17 (.D(i17), .en(we), .Q(o17), .clk(in_1), .clr(rst));
  Register #(.width(32)) r18 (.D(i18), .en(we), .Q(o18), .clk(in_1), .clr(rst));
  Register #(.width(32)) r19 (.D(i19), .en(we), .Q(o19), .clk(in_1), .clr(rst));
  Register #(.width(32)) r20 (.D(i20), .en(we), .Q(o20), .clk(in_1), .clr(rst));
  Register #(.width(32)) r21 (.D(i21), .en(we), .Q(o21), .clk(in_1), .clr(rst));
  Register #(.width(32)) r22 (.D(i22), .en(we), .Q(o22), .clk(in_1), .clr(rst));
  Register #(.width(32)) r23 (.D(i23), .en(we), .Q(o23), .clk(in_1), .clr(rst));
  Register #(.width(32)) r24 (.D(i24), .en(we), .Q(o24), .clk(in_1), .clr(rst));
  Register #(.width(32)) r25 (.D(i25), .en(we), .Q(o25), .clk(in_1), .clr(rst));
  Register #(.width(32)) r26 (.D(i26), .en(we), .Q(o26), .clk(in_1), .clr(rst));
  Register #(.width(32)) r27 (.D(i27), .en(we), .Q(o27), .clk(in_1), .clr(rst));
  Register #(.width(32)) r28 (.D(i28), .en(we), .Q(o28), .clk(in_1), .clr(rst));
  Register #(.width(32)) r29 (.D(i29), .en(we), .Q(o29), .clk(in_1), .clr(rst));
  Register #(.width(32)) r30 (.D(i30), .en(we), .Q(o30), .clk(in_1), .clr(rst));
  Register #(.width(32)) r31 (.D(i31), .en(we), .Q(o31), .clk(in_1), .clr(rst));
  Multiplexer #(.select(5), .width(32)) multiplexer_1 (
    .in0(o0), .in1(o1), .in2(o2), .in3(o3), .in4(o4), .in5(o5), .in6(o6), .in7(o7), .in8(o8), .in9(o9),
    .in10(o10), .in11(o11), .in12(o12), .in13(o13), .in14(o14), .in15(o15), .in16(o16), .in17(o17),
    .in18(o18), .in19(o19), .in20(o20), .in21(o21), .in22(o22), .in23(o23), .in24(o24), .in25(o25),
    .in26(o26), .in27(o27), .in28(o28), .in29(o29), .in30(o30), .in31(o31), .out(RD1), .sel(A1));  // open: en
  Multiplexer #(.select(5), .width(32)) multiplexer_2 (
    .in0(o0), .in1(o1), .in2(o2), .in3(o3), .in4(o4), .in5(o5), .in6(o6), .in7(o7), .in8(o8), .in9(o9),
    .in10(o10), .in11(o11), .in12(o12), .in13(o13), .in14(o14), .in15(o15), .in16(o16), .in17(o17),
    .in18(o18), .in19(o19), .in20(o20), .in21(o21), .in22(o22), .in23(o23), .in24(o24), .in25(o25),
    .in26(o26), .in27(o27), .in28(o28), .in29(o29), .in30(o30), .in31(o31), .out(RD2), .sel(A2));  // open: en
  Demultiplexer #(.select(5), .width(32), .tristate("true")) demultiplexer_1 (
    .out0(i0), .out1(i1), .out2(i2), .out3(i3), .out4(i4), .out5(i5), .out6(i6), .out7(i7), .out8(i8),
    .out9(i9), .out10(i10), .out11(i11), .out12(i12), .out13(i13), .out14(i14), .out15(i15), .out16(i16),
    .out17(i17), .out18(i18), .out19(i19), .out20(i20), .out21(i21), .out22(i22), .out23(i23), .out24(i24),
    .out25(i25), .out26(i26), .out27(i27), .out28(i28), .out29(i29), .out30(i30), .out31(i31), .in(WD),
    .sel(A3));  // open: en

  // Other names for the same wires on the sheet: clk = in_1
endmodule

module EXT (
  input  [15:0] in_1,
  input  \signed ,
  output [31:0] out
);

  wire [31:0] bit_extender_1_out, bit_extender_2_out;

  assign bit_extender_1_out = {{16{1'b0}}, in_1};  // Bit_Extender bit_extender_1
  assign bit_extender_2_out = {{16{in_1[15]}}, in_1};  // Bit_Extender bit_extender_2
  Multiplexer #(.width(32)) multiplexer_1 (
    .in0(bit_extender_1_out), .in1(bit_extender_2_out), .out(out), .sel(\signed ));  // open: en
endmodule

module ALU (
  input  [3:0] ALUControl,
  input  [31:0] SrcA,
  input  [31:0] SrcB,
  input  [4:0] shamt,
  output zero,
  output [31:0] Result
);

  wire comparator_1_lt, comparator_2_eq, comparator_2_lt, or_2_out;
  wire [31:0] adder_1_out, and_1_out, bit_extender_1_out, bit_extender_2_out, or_1_out, shifter_1_out,
       shifter_2_out, shifter_3_out, subtractor_1_out;

  Adder #(.width(32)) adder_1 (.a(SrcA), .b(SrcB), .out(adder_1_out));  // open: cin, cout
  Subtractor #(.width(32)) subtractor_1 (.a(SrcA), .b(SrcB), .out(subtractor_1_out));  // open: bin, bout
  assign and_1_out = SrcA & SrcB;  // AND_Gate and_1, 32 bits wide
  assign or_1_out = SrcA | SrcB;  // OR_Gate or_1, 32 bits wide
  Comparator #(.width(32), .mode("unsigned")) comparator_1 (.a(SrcA), .b(SrcB), .lt(comparator_1_lt));  // open: gt, eq
  Comparator #(.width(32)) comparator_2 (.a(SrcA), .b(SrcB), .eq(comparator_2_eq), .lt(comparator_2_lt));  // open: gt
  Shifter #(.width(32)) shifter_1 (.in(SrcB), .\dist (shamt), .out(shifter_1_out));
  assign bit_extender_1_out = {{31{1'b0}}, comparator_1_lt};  // Bit_Extender bit_extender_1
  Shifter #(.width(32)) shifter_2 (.in(SrcB), .\dist (5'b10000), .out(shifter_2_out));
  Shifter #(.width(32)) shifter_3 (.in(SrcB), .\dist (SrcA[4:0]), .out(shifter_3_out));
  or or_2 (or_2_out, comparator_2_eq, comparator_2_lt);
  assign bit_extender_2_out = {{31{1'b0}}, or_2_out};  // Bit_Extender bit_extender_2
  Multiplexer #(.select(4), .width(32)) multiplexer_1 (
    .in0(adder_1_out), .in1(subtractor_1_out), .in2(and_1_out), .in3(or_1_out), .in4(shifter_1_out),
    .in5(bit_extender_1_out), .in6(shifter_2_out), .in7(shifter_3_out), .in8(bit_extender_2_out),
    .out(Result), .sel(ALUControl));  // open: in9, in10, in11, in12, in13, in14, in15, en
  Comparator #(.width(32), .mode("unsigned")) comparator_3 (.a({32{1'b0}}), .b(Result), .eq(zero));  // open: gt, lt
endmodule

module DM (
  input  we,
  input  [4:0] A,
  input  [31:0] WD,
  input  in_4,
  input  rst,
  output [31:0] RD
);

  RAM #(.addrWidth(5), .dataWidth(32), .bus("separate")) ram_1 (
    .addr(A), .din(WD), .data(RD), .str(we), .clk(in_4), .clr(rst));  // open: sel, ld
endmodule

module MR (
  input  [31:0] addr,
  input  [2:0] \type ,
  input  [31:0] data,
  output [31:0] out_4
);

  wire [15:0] multiplexer_1_out, multiplexer_2_out;
  wire [31:0] lh, lhu;

  assign lh = {{16{multiplexer_1_out[15]}}, multiplexer_1_out};  // Bit_Extender bit_extender_1
  Multiplexer #(.width(16)) multiplexer_1 (
    .in0(data[15:0]), .in1(data[31:16]), .out(multiplexer_1_out), .sel(addr[1]));  // open: en
  assign lhu = {{16{1'b0}}, multiplexer_2_out};  // Bit_Extender bit_extender_2
  Multiplexer #(.width(16)) multiplexer_2 (
    .in0(data[15:0]), .in1(data[31:16]), .out(multiplexer_2_out), .sel(addr[1]));  // open: en
  Multiplexer #(.select(3), .width(32)) multiplexer_3 (
    .in0(data), .in1(lh), .in2(lhu), .out(out_4), .sel(\type ));  // open: in3, in4, in5, in6, in7, en

  // Other names for the same wires on the sheet: lw[31:0] = data
endmodule

module MW (
  input  [31:0] addr,
  input  [2:0] \type ,
  input  [31:0] ALUdata,
  input  [31:0] oldData,
  output [31:0] out_5
);

  wire [15:0] multiplexer_1_out;
  wire [31:0] bit_extender_1_out, bit_extender_2_out, or_1_out, or_2_out, sh, shifter_1_out, shifter_2_out;

  Multiplexer #(.width(16)) multiplexer_1 (
    .in0(oldData[31:16]), .in1(oldData[15:0]), .out(multiplexer_1_out), .sel(addr[1]));  // open: en
  Multiplexer #(.select(3), .width(32)) multiplexer_2 (
    .in0(ALUdata), .in1(sh), .out(out_5), .sel(\type ));  // open: in2, in3, in4, in5, in6, in7, en
  assign bit_extender_1_out = {{16{1'b0}}, multiplexer_1_out};  // Bit_Extender bit_extender_1
  assign bit_extender_2_out = {{16{1'b0}}, ALUdata[15:0]};  // Bit_Extender bit_extender_2
  Shifter #(.width(32)) shifter_1 (.in(bit_extender_1_out), .\dist (5'b10000), .out(shifter_1_out));
  Shifter #(.width(32)) shifter_2 (.in(bit_extender_2_out), .\dist (5'b10000), .out(shifter_2_out));
  assign or_1_out = shifter_1_out | bit_extender_2_out;  // OR_Gate or_1, 32 bits wide
  assign or_2_out = bit_extender_1_out | shifter_2_out;  // OR_Gate or_2, 32 bits wide
  Multiplexer #(.width(32)) multiplexer_3 (.in0(or_1_out), .in1(or_2_out), .out(sh), .sel(addr[1]));  // open: en

  // Other names for the same wires on the sheet: sw[31:0] = ALUdata
endmodule

module NPC (
  input  [31:0] PC,
  input  [25:0] IMM26,
  input  [31:0] RA,
  input  [2:0] Br,
  input  ALUZero,
  output [31:0] out_6,
  output [31:0] PC4
);

  wire [31:0] adder_2_out, bit_extender_1_out, multiplexer_1_out, shifter_1_out;

  assign bit_extender_1_out = {{16{IMM26[15]}}, IMM26[15:0]};  // Bit_Extender bit_extender_1
  Adder #(.width(32)) adder_1 (.a(PC), .b(32'h4), .out(PC4));  // open: cin, cout
  Shifter #(.width(32)) shifter_1 (.in(bit_extender_1_out), .\dist (5'b00010), .out(shifter_1_out));
  Adder #(.width(32)) adder_2 (.a(PC4), .b(shifter_1_out), .out(adder_2_out));  // open: cin, cout
  Multiplexer #(.width(32)) multiplexer_1 (
    .in0(PC4), .in1(adder_2_out), .out(multiplexer_1_out), .sel(ALUZero));  // open: en
  Multiplexer #(.select(3), .width(32)) multiplexer_2 (
    .in0(PC4), .in1(multiplexer_1_out), .in2({PC[31:28], IMM26, 2'b00}), .in3({PC[31:28], IMM26, 2'b00}),
    .in4(RA), .out(out_6), .sel(Br));  // open: in5, in6, in7, en

  // Other names for the same wires on the sheet: NPC[31:0] = out_6
endmodule

module CU (
  input  [31:0] in_1,
  output [2:0] DMType,
  output [2:0] Br,
  output [1:0] A3Sel,
  output [1:0] WDSel,
  output RFWr,
  output EXTOp,
  output BSel,
  output DMWr,
  output [3:0] ALUControl
);

  wire _branch, _load, addi, addu, \and , beq, blez, comparator_1_eq, comparator_2_eq, comparator_3_eq,
       comparator_4_eq, comparator_5_eq, comparator_6_eq, comparator_7_eq, comparator_8_eq, j, jal, jr, lh,
       lhu, lui, lw, \or , or_1_out, or_2_out, or_3_out, or_4_out, or_5_out, or_6_out, or_7_out, or_8_out,
       or_9_out, or_11_out, or_12_out, or_13_out, or_14_out, ori, r, sh, sll, sllv, slt, slti, subu, sw;

  Comparator #(.width(6)) comparator_1 (.a(in_1[5:0]), .b(6'b100001), .eq(comparator_1_eq));  // open: gt, lt
  Comparator #(.width(6)) comparator_2 (.a(in_1[5:0]), .b(6'b100011), .eq(comparator_2_eq));  // open: gt, lt
  Comparator #(.width(6)) comparator_3 (.a(in_1[5:0]), .b(6'b100100), .eq(comparator_3_eq));  // open: gt, lt
  Comparator #(.width(6)) comparator_4 (.a(in_1[5:0]), .b(6'b100111), .eq(comparator_4_eq));  // open: gt, lt
  Comparator #(.width(6)) comparator_5 (.a(in_1[5:0]), .b({6{1'b0}}), .eq(comparator_5_eq));  // open: gt, lt
  Comparator #(.width(6)) comparator_6 (.a(in_1[5:0]), .b(6'b000100), .eq(comparator_6_eq));  // open: gt, lt
  Comparator #(.width(6)) comparator_7 (.a(in_1[5:0]), .b(6'b101010), .eq(comparator_7_eq));  // open: gt, lt
  Comparator #(.width(6)) comparator_8 (.a(in_1[5:0]), .b(6'b001000), .eq(comparator_8_eq));  // open: gt, lt
  Comparator #(.width(6)) comparator_9 (.a(in_1[31:26]), .b({6{1'b0}}), .eq(r));  // open: gt, lt
  and and_1 (addu, comparator_1_eq, r);
  and and_2 (subu, comparator_2_eq, r);
  and and_3 (\and , comparator_3_eq, r);
  and and_4 (\or , comparator_4_eq, r);
  and and_5 (sll, comparator_5_eq, r);
  and and_6 (sllv, comparator_6_eq, r);
  and and_7 (slt, comparator_7_eq, r);
  and and_8 (jr, comparator_8_eq, r);
  Comparator #(.width(6)) comparator_10 (.a(in_1[31:26]), .b(6'b001000), .eq(addi));  // open: gt, lt
  Comparator #(.width(6)) comparator_11 (.a(in_1[31:26]), .b(6'b001101), .eq(ori));  // open: gt, lt
  Comparator #(.width(6)) comparator_12 (.a(in_1[31:26]), .b(6'b001111), .eq(lui));  // open: gt, lt
  Comparator #(.width(6)) comparator_13 (.a(in_1[31:26]), .b(6'b001010), .eq(slti));  // open: gt, lt
  or or_1 (or_1_out, lw, sw);
  or or_2 (or_2_out, lh, sh);
  or or_3 (or_3_out, subu, beq);
  buf or_4 (or_4_out, \and );  // OR_Gate
  or or_5 (or_5_out, \or , ori);
  buf or_6 (or_6_out, sll);  // OR_Gate
  or or_7 (or_7_out, slt, slti);
  buf or_8 (or_8_out, sllv);  // OR_Gate
  buf or_9 (or_9_out, jal);  // OR_Gate
  buf or_10 (_branch, beq);  // OR_Gate
  Comparator #(.width(6)) comparator_14 (.a(in_1[31:26]), .b(6'b000100), .eq(beq));  // open: gt, lt
  Pull_Resistor pull_resistor_1 (.node(ALUControl));
  Priority_Encoder #(.select(4)) priority_encoder_1 (
    .in1(or_3_out), .in2(or_4_out), .in3(or_5_out), .in4(or_6_out), .in5(or_7_out), .in6(lui),
    .in7(or_8_out), .in8(blez), .out(ALUControl));  // open: in0, in9, in10, in11, in12, in13, in14, in15, gs, en_out, en_in
  Priority_Encoder #(.select(2)) priority_encoder_2 (
    .in1(r), .in2(or_9_out), .out(A3Sel));  // open: in0, in3, gs, en_out, en_in
  Pull_Resistor pull_resistor_2 (.node(A3Sel));
  nor nor_1 (RFWr, DMWr, _branch, j, jr);
  nor nor_2 (BSel, r, _branch, j, jal);
  Pull_Resistor pull_resistor_3 (.node(DMType));
  Priority_Encoder priority_encoder_3 (
    .in0(or_1_out), .in1(or_2_out), .in2(lhu), .out(DMType));  // open: in3, in4, in5, in6, in7, en_in, gs, en_out
  Comparator #(.width(6)) comparator_15 (.a(in_1[31:26]), .b(6'b000010), .eq(j));  // open: gt, lt
  Comparator #(.width(6)) comparator_16 (.a(in_1[31:26]), .b(6'b000011), .eq(jal));  // open: gt, lt
  buf or_11 (or_11_out, beq);  // OR_Gate
  buf or_12 (or_12_out, jal);  // OR_Gate
  buf or_13 (or_13_out, jr);  // OR_Gate
  buf or_14 (or_14_out, jal);  // OR_Gate
  or or_15 (DMWr, sw, sh);
  Comparator #(.width(6)) comparator_17 (.a(in_1[31:26]), .b(6'b101011), .eq(sw));  // open: gt, lt
  Comparator #(.width(6)) comparator_18 (.a(in_1[31:26]), .b(6'b101001), .eq(sh));  // open: gt, lt
  or or_16 (EXTOp, DMWr, addi, _load);
  Priority_Encoder priority_encoder_4 (
    .in1(or_11_out), .in2(j), .in3(or_12_out), .in4(or_13_out), .out(Br));  // open: in0, in5, in6, in7, en_in, gs, en_out
  Pull_Resistor pull_resistor_4 (.node(Br));
  Priority_Encoder #(.select(2)) priority_encoder_5 (
    .in1(_load), .in2(or_14_out), .out(WDSel));  // open: in0, in3, gs, en_out, en_in
  Pull_Resistor pull_resistor_5 (.node(WDSel));
  or or_17 (_load, lw, lh, lhu);
  Comparator #(.width(6)) comparator_19 (.a(in_1[31:26]), .b(6'b100011), .eq(lw));  // open: gt, lt
  Comparator #(.width(6)) comparator_20 (.a(in_1[31:26]), .b(6'b100001), .eq(lh));  // open: gt, lt
  Comparator #(.width(6)) comparator_21 (.a(in_1[31:26]), .b(6'b100101), .eq(lhu));  // open: gt, lt

  // Other names for the same wires on the sheet: _store = DMWr; func[5:0] = in_1[5:0]; opcode[5:0] = in_1[31:26]
endmodule
